// Logisim project ALU3.circ as structural Verilog
module ALU_Unit (
  input  [5:0] in_1,
  input  [31:0] in_2,
  input  [31:0] in_3,
  output [31:0] out_4,
  output out_5,
  output out_6
);

  wire [31:0] Arth_Result, Logic_Result, SET_SSET_Result, Shift_Result;

  Shifter_Unit shifter_unit_1 (.in_2(in_2), .in_3(in_3), .out_4(Shift_Result), .OperationControl(in_1[3:0]));
  Arthimetic_Unit arthimetic_unit_1 (
    .RS1_RD(in_2), .RS2_imm32(in_3), .out_4(Arth_Result), .out_5(out_5), .out_6(out_6),
    .OperationControl(in_1[3:0]));
  Logical_Unit logical_unit_1 (.RS1_RD(in_2), .RS2_imm32(in_3), .out_4(Logic_Result), .OperationControl(in_1[3:0]));
  Multiplexer #(.width(32), .enable("false")) multiplexer_1 (
    .in0(in_3), .in1({in_2[15:0], in_3[15:0]}), .out(SET_SSET_Result), .sel(in_1[0]));
  Multiplexer #(.select(2), .width(32), .enable("false")) multiplexer_2 (
    .in0(Shift_Result), .in1(Arth_Result), .in2(Logic_Result), .in3(SET_SSET_Result), .out(out_4),
    .sel(in_1[5:4]));

  // Other names for the same wires on the sheet: A[31:0] = in_2; ALU_Operation[5:0] = in_1;
  //   OperationControl[3:0] = in_1[3:0]; ALUResult_Selection[1:0] = in_1[5:4]; overflow = out_6; B[31:0] = in_3;
  //   SET[31:0] = in_3; SSET[31:0] = {in_2[15:0], in_3[15:0]}; zero = out_5

  // Notes on the sheet:
  //   Inputs
  //   ALU_OperationContol
  //   Units
  //   Output
endmodule

module Arthimetic_Unit (
  input  [3:0] OperationControl,
  input  [31:0] RS1_RD,
  input  [31:0] RS2_imm32,
  output [31:0] out_4,
  output out_5,
  output out_6
);

  wire adder_1_cout, adder_2_cout, comparator_1_lt, xor_2_out;
  wire [31:0] ADD_SUB, ADD_SUB_MUL, bit_extender_1_out, MUL, SEQ, SLT, SLTU, xor_1_out;

  assign xor_1_out = RS2_imm32 ^ bit_extender_1_out;  // XOR_Gate xor_1, 32 bits wide
  assign bit_extender_1_out = {{31{OperationControl[3]}}, OperationControl[3]};  // Bit_Extender bit_extender_1
  Adder #(.width(31)) adder_1 (
    .a(RS1_RD[30:0]), .b(xor_1_out[30:0]), .out(ADD_SUB[30:0]), .cin(OperationControl[3]), .cout(adder_1_cout));
  Adder #(.width(1)) adder_2 (
    .a(RS1_RD[31]), .b(xor_1_out[31]), .out(ADD_SUB[31]), .cin(adder_1_cout), .cout(adder_2_cout));
  xor xor_2 (xor_2_out, ADD_SUB[31], out_6);
  Comparator #(.width(32), .mode("unsigned")) comparator_1 (
    .a(RS1_RD), .b(RS2_imm32), .lt(comparator_1_lt));  // open: gt, eq
  Multiplier #(.width(32)) multiplier_1 (.a(RS1_RD), .b(RS2_imm32), .out(MUL));  // open: cin, cout
  assign SLT = {{31{1'b0}}, xor_2_out};  // Bit_Extender bit_extender_2
  assign SLTU = {{31{1'b0}}, comparator_1_lt};  // Bit_Extender bit_extender_3
  assign SEQ = {{31{1'b0}}, out_5};  // Bit_Extender bit_extender_4
  xor xor_3 (out_6, adder_1_cout, adder_2_cout);
  Multiplexer #(.width(32), .enable("false")) multiplexer_1 (
    .in0(ADD_SUB), .in1(MUL), .out(ADD_SUB_MUL), .sel(OperationControl[2]));
  nor nor_1 (out_5, ADD_SUB[0], ADD_SUB[1], ADD_SUB[2], ADD_SUB[3], ADD_SUB[4], ADD_SUB[5], ADD_SUB[6], ADD_SUB[7], ADD_SUB[8], ADD_SUB[9], ADD_SUB[10], ADD_SUB[11], ADD_SUB[12], ADD_SUB[13], ADD_SUB[14], ADD_SUB[15], ADD_SUB[16], ADD_SUB[17], ADD_SUB[18], ADD_SUB[19], ADD_SUB[20], ADD_SUB[21], ADD_SUB[22], ADD_SUB[23], ADD_SUB[24], ADD_SUB[25], ADD_SUB[26], ADD_SUB[27], ADD_SUB[28], ADD_SUB[29], ADD_SUB[30], ADD_SUB[31]);
  Multiplexer #(.select(2), .width(32)) multiplexer_2 (
    .in0(ADD_SUB_MUL), .in1(SLT), .in2(SLTU), .in3(SEQ), .out(out_4), .sel(OperationControl[1:0]));  // open: en

  // Other names for the same wires on the sheet: A[31:0] = RS1_RD; Sign = ADD_SUB[31]; B[31:0] = RS2_imm32;
  //   Result_Selection[1:0] = OperationControl[1:0]; ArthOp = OperationControl[2]; AluOp_1_bit = OperationControl[3];
  //   Overflow = out_6; Zero = out_5

  // Notes on the sheet:
  //   Inputs
  //   ADD/SUB_Signal
  //   ArthOpSignal
  //   Operations
  //   data out
  //   zero_Detection
  //   outputs
endmodule

module Logical_Unit (
  input  [3:0] OperationControl,
  input  [31:0] RS1_RD,
  input  [31:0] RS2_imm32,
  output [31:0] out_4
);

  wire [31:0] AND, NOR, OR, XOR;

  assign AND = RS1_RD & RS2_imm32;  // AND_Gate and_1, 32 bits wide
  assign OR = RS1_RD | RS2_imm32;  // OR_Gate or_1, 32 bits wide
  assign XOR = RS1_RD ^ RS2_imm32;  // XOR_Gate xor_1, 32 bits wide
  assign NOR = ~OR;  // NOT_Gate not_1, 32 bits wide
  Multiplexer #(.select(2), .width(32), .enable("false")) multiplexer_1 (
    .in0(AND), .in1(OR), .in2(NOR), .in3(XOR), .out(out_4), .sel(OperationControl[1:0]));

  // Other names for the same wires on the sheet: A[31:0] = RS1_RD; B[31:0] = RS2_imm32;
  //   Result_Selection[1:0] = OperationControl[1:0]; ArthOp = OperationControl[2]; AluOp_1_bit = OperationControl[3]

  // Notes on the sheet:
  //   Inputs
  //   ADD/SUB_Signal
  //   ArthOpSignal
  //   Operations
  //   Output
endmodule

module Shifter_Unit (
  input  [3:0] OperationControl,
  input  [31:0] in_2,
  input  [31:0] in_3,
  output [31:0] out_4
);

  wire [31:0] Arhimetic_Right, Logical_Left, Logical_Right, Rotate_Right;

  Shifter #(.width(32)) shifter_1 (.in(in_2), .\dist (in_3[4:0]), .out(Logical_Left));
  Shifter #(.width(32), .shift("lr")) shifter_2 (.in(in_2), .\dist (in_3[4:0]), .out(Logical_Right));
  Shifter #(.width(32), .shift("ar")) shifter_3 (.in(in_2), .\dist (in_3[4:0]), .out(Arhimetic_Right));
  Shifter #(.width(32), .shift("rr")) shifter_4 (.in(in_2), .\dist (in_3[4:0]), .out(Rotate_Right));
  Multiplexer #(.select(2), .width(32), .enable("false")) multiplexer_1 (
    .in0(Logical_Left), .in1(Logical_Right), .in2(Arhimetic_Right), .in3(Rotate_Right), .out(out_4),
    .sel(OperationControl[1:0]));

  // Other names for the same wires on the sheet: A[31:0] = in_2; Shift_Amount[4:0] = in_3[4:0];
  //   Result_Selection[1:0] = OperationControl[1:0]; ArthOp = OperationControl[2]; AluOp_1_bit = OperationControl[3]

  // Notes on the sheet:
  //   Inputs
  //   ADD/SUB_Signal
  //   ArthOpSignal
  //   Operations
  //   Output
endmodule
