// Logisim project i_type_datapath.circ as structural Verilog
module ALU_Unit (
  input  [5:0] in_1,
  input  [31:0] in_2,
  input  [31:0] in_3,
  output [31:0] out_4,
  output out_5,
  output out_6
);

  wire [31:0] Arth_Result, Logic_Result, SET_SSET_Result, Shift_Result;

  Shifter_Unit shifter_unit_1 (.in_2(in_2), .in_3(in_3), .out_4(Shift_Result), .OperationControl(in_1[3:0]));
  Arthimetic_Unit arthimetic_unit_1 (
    .RS1_RD(in_2), .RS2_imm32(in_3), .out_4(Arth_Result), .out_5(out_5), .out_6(out_6),
    .OperationControl(in_1[3:0]));
  Logical_Unit logical_unit_1 (.RS1_RD(in_2), .RS2_imm32(in_3), .out_4(Logic_Result), .OperationControl(in_1[3:0]));
  Multiplexer #(.width(32), .enable("false")) multiplexer_1 (
    .in0(in_3), .in1({in_2[15:0], in_3[15:0]}), .out(SET_SSET_Result), .sel(in_1[0]));
  Multiplexer #(.select(2), .width(32), .enable("false")) multiplexer_2 (
    .in0(Shift_Result), .in1(Arth_Result), .in2(Logic_Result), .in3(SET_SSET_Result), .out(out_4),
    .sel(in_1[5:4]));

  // Other names for the same wires on the sheet: A[31:0] = in_2; ALU_Operation[5:0] = in_1;
  //   OperationControl[3:0] = in_1[3:0]; ALUResult_Selection[1:0] = in_1[5:4]; overflow = out_6; B[31:0] = in_3;
  //   SET[31:0] = in_3; SSET[31:0] = {in_2[15:0], in_3[15:0]}; zero = out_5

  // Notes on the sheet:
  //   Inputs
  //   ALU_OperationContol
  //   Units
  //   Output
endmodule

module Arthimetic_Unit (
  input  [3:0] OperationControl,
  input  [31:0] RS1_RD,
  input  [31:0] RS2_imm32,
  output [31:0] out_4,
  output out_5,
  output out_6
);

  wire adder_1_cout, adder_2_cout, comparator_1_lt, xor_2_out;
  wire [31:0] ADD_SUB, ADD_SUB_MUL, bit_extender_1_out, MUL, SEQ, SLT, SLTU, xor_1_out;

  assign xor_1_out = RS2_imm32 ^ bit_extender_1_out;  // XOR_Gate xor_1, 32 bits wide
  assign bit_extender_1_out = {{31{OperationControl[3]}}, OperationControl[3]};  // Bit_Extender bit_extender_1
  Adder #(.width(31)) adder_1 (
    .a(RS1_RD[30:0]), .b(xor_1_out[30:0]), .out(ADD_SUB[30:0]), .cin(OperationControl[3]), .cout(adder_1_cout));
  Adder #(.width(1)) adder_2 (
    .a(RS1_RD[31]), .b(xor_1_out[31]), .out(ADD_SUB[31]), .cin(adder_1_cout), .cout(adder_2_cout));
  xor xor_2 (xor_2_out, ADD_SUB[31], out_6);
  Comparator #(.width(32), .mode("unsigned")) comparator_1 (
    .a(RS1_RD), .b(RS2_imm32), .lt(comparator_1_lt));  // open: gt, eq
  Multiplier #(.width(32)) multiplier_1 (.a(RS1_RD), .b(RS2_imm32), .out(MUL));  // open: cin, cout
  assign SLT = {{31{1'b0}}, xor_2_out};  // Bit_Extender bit_extender_2
  assign SLTU = {{31{1'b0}}, comparator_1_lt};  // Bit_Extender bit_extender_3
  assign SEQ = {{31{1'b0}}, out_5};  // Bit_Extender bit_extender_4
  xor xor_3 (out_6, adder_1_cout, adder_2_cout);
  Multiplexer #(.width(32), .enable("false")) multiplexer_1 (
    .in0(ADD_SUB), .in1(MUL), .out(ADD_SUB_MUL), .sel(OperationControl[2]));
  nor nor_1 (out_5, ADD_SUB[0], ADD_SUB[1], ADD_SUB[2], ADD_SUB[3], ADD_SUB[4], ADD_SUB[5], ADD_SUB[6], ADD_SUB[7], ADD_SUB[8], ADD_SUB[9], ADD_SUB[10], ADD_SUB[11], ADD_SUB[12], ADD_SUB[13], ADD_SUB[14], ADD_SUB[15], ADD_SUB[16], ADD_SUB[17], ADD_SUB[18], ADD_SUB[19], ADD_SUB[20], ADD_SUB[21], ADD_SUB[22], ADD_SUB[23], ADD_SUB[24], ADD_SUB[25], ADD_SUB[26], ADD_SUB[27], ADD_SUB[28], ADD_SUB[29], ADD_SUB[30], ADD_SUB[31]);
  Multiplexer #(.select(2), .width(32)) multiplexer_2 (
    .in0(ADD_SUB_MUL), .in1(SLT), .in2(SLTU), .in3(SEQ), .out(out_4), .sel(OperationControl[1:0]));  // open: en

  // Other names for the same wires on the sheet: A[31:0] = RS1_RD; Sign = ADD_SUB[31]; B[31:0] = RS2_imm32;
  //   Result_Selection[1:0] = OperationControl[1:0]; ArthOp = OperationControl[2]; AluOp_1_bit = OperationControl[3];
  //   Overflow = out_6; Zero = out_5

  // Notes on the sheet:
  //   Inputs
  //   ADD/SUB_Signal
  //   ArthOpSignal
  //   Operations
  //   data out
  //   zero_Detection
  //   outputs
endmodule

module Logical_Unit (
  input  [3:0] OperationControl,
  input  [31:0] RS1_RD,
  input  [31:0] RS2_imm32,
  output [31:0] out_4
);

  wire [31:0] AND, NOR, OR, XOR;

  assign AND = RS1_RD & RS2_imm32;  // AND_Gate and_1, 32 bits wide
  assign OR = RS1_RD | RS2_imm32;  // OR_Gate or_1, 32 bits wide
  assign XOR = RS1_RD ^ RS2_imm32;  // XOR_Gate xor_1, 32 bits wide
  assign NOR = ~OR;  // NOT_Gate not_1, 32 bits wide
  Multiplexer #(.select(2), .width(32), .enable("false")) multiplexer_1 (
    .in0(AND), .in1(OR), .in2(NOR), .in3(XOR), .out(out_4), .sel(OperationControl[1:0]));

  // Other names for the same wires on the sheet: A[31:0] = RS1_RD; B[31:0] = RS2_imm32;
  //   Result_Selection[1:0] = OperationControl[1:0]; ArthOp = OperationControl[2]; AluOp_1_bit = OperationControl[3]

  // Notes on the sheet:
  //   Inputs
  //   ADD/SUB_Signal
  //   ArthOpSignal
  //   Operations
  //   Output
endmodule

module Shifter_Unit (
  input  [3:0] OperationControl,
  input  [31:0] in_2,
  input  [31:0] in_3,
  output [31:0] out_4
);

  wire [31:0] Arhimetic_Right, Logical_Left, Logical_Right, Rotate_Right;

  Shifter #(.width(32)) shifter_1 (.in(in_2), .\dist (in_3[4:0]), .out(Logical_Left));
  Shifter #(.width(32), .shift("lr")) shifter_2 (.in(in_2), .\dist (in_3[4:0]), .out(Logical_Right));
  Shifter #(.width(32), .shift("ar")) shifter_3 (.in(in_2), .\dist (in_3[4:0]), .out(Arhimetic_Right));
  Shifter #(.width(32), .shift("rr")) shifter_4 (.in(in_2), .\dist (in_3[4:0]), .out(Rotate_Right));
  Multiplexer #(.select(2), .width(32), .enable("false")) multiplexer_1 (
    .in0(Logical_Left), .in1(Logical_Right), .in2(Arhimetic_Right), .in3(Rotate_Right), .out(out_4),
    .sel(OperationControl[1:0]));

  // Other names for the same wires on the sheet: A[31:0] = in_2; Shift_Amount[4:0] = in_3[4:0];
  //   Result_Selection[1:0] = OperationControl[1:0]; ArthOp = OperationControl[2]; AluOp_1_bit = OperationControl[3]

  // Notes on the sheet:
  //   Inputs
  //   ADD/SUB_Signal
  //   ArthOpSignal
  //   Operations
  //   Output
endmodule

module DataPath_I_Type (
  input  [1:0] in_1,
  input  in_2,
  input  in_3,
  input  [5:0] in_4,
  input  in_5,
  input  in_6,
  input  in_7,
  input  in_8
);

  wire clk, Overflow, ZeroF;
  wire [4:0] d, multiplexer_2_out, S1;
  wire [5:0] OP;
  wire [15:0] imm16;
  wire [19:0] multiplexer_1_out, pc, pc_1;
  wire [31:0] A, ALUD, bit_extender_1_out, imm32, ram_1_data, WB;

  Multiplexer #(.width(20), .enable("false")) multiplexer_1 (
    .in0(pc_1), .in1(ALUD[19:0]), .out(multiplexer_1_out), .sel(in_8));
  adder_1 adder_1_1 (.in_1(pc), .out_2(pc_1));
  Register #(.width(20)) register_1 (.D(multiplexer_1_out), .Q(pc), .clk(clk));  // open: en, clr
  ROM #(.addrWidth(20), .dataWidth(32)) rom_1 (.addr(pc), .data({imm16, S1, d, OP}));  // open: sel
  extender extender_1 (.in_1(imm16), .out_3(imm32), .in_2(in_7));
  Multiplexer #(.width(5), .enable("false")) multiplexer_2 (.in0(S1), .in1(d), .out(multiplexer_2_out), .sel(in_5));
  Register_File register_file_1 (
    .RA(multiplexer_2_out), .in_6(clk), .BusA(A), .RW(d), .RegWrite(in_6), .BusW(WB));  // open: RB, BusB
  ALU_Unit alu_unit_1 (.in_2(A), .in_3(imm32), .out_4(ALUD), .out_5(ZeroF), .out_6(Overflow), .in_1(in_4));
  Clock clock_1 (.out(clk));
  RAM #(.addrWidth(20), .dataWidth(32), .bus("separate")) ram_1 (
    .addr(ALUD[19:0]), .data(ram_1_data), .str(in_2), .clk(clk), .ld(in_3));  // open: din, sel, clr
  assign bit_extender_1_out = {{12{1'b0}}, pc_1};  // Bit_Extender bit_extender_1
  Multiplexer #(.select(2), .width(32), .enable("false")) multiplexer_3 (
    .in0(ALUD), .in1(ram_1_data), .in2(bit_extender_1_out), .out(WB), .sel(in_1));  // open: in3

  // Other names for the same wires on the sheet: Sa[4:0] = imm16[4:0]; AluOpCtrl[5:0] = in_4; pcNext = in_8;
  //   ReadSignal = in_3; RegWrite = in_6; signSlc = in_7; sourceSlc = in_5; WBSlc[1:0] = in_1; WriteSgnal = in_2

  // Notes on the sheet:
  //   pc
  //   IM
  //   contents of rom_1 (hex, n*v repeats v):
  //   0 f00cd f1c8f 4010d 5014d 2008d 1004d 20190 20190 fff901ce 51901 51a01 33242 21a83 732c4 fffb1b05
  //   fffb1046 fffb1047 fffe1b48 fff82389 fff823ca fff8240b fff8244c 5148f
  //   Control Unit Signals
  //   DM
  //   writebackSlc
endmodule

module extender (
  input  [15:0] in_1,
  input  in_2,
  output [31:0] out_3
);

  wire [31:0] bit_extender_1_out, bit_extender_2_out;

  assign bit_extender_1_out = {{16{1'b0}}, in_1};  // Bit_Extender bit_extender_1
  assign bit_extender_2_out = {{16{in_1[15]}}, in_1};  // Bit_Extender bit_extender_2
  Multiplexer #(.width(32)) multiplexer_1 (
    .in0(bit_extender_1_out), .in1(bit_extender_2_out), .out(out_3), .sel(in_2));  // open: en
endmodule

module adder_1 (
  input  [19:0] in_1,
  output [19:0] out_2
);

  wire [19:0] bit_extender_1_out;

  assign bit_extender_1_out = {{19{1'b0}}, 1'b1};  // Bit_Extender bit_extender_1
  Adder #(.width(20)) adder_1 (.a(in_1), .b(bit_extender_1_out), .out(out_2), .cin(1'b0));  // open: cout

  // Notes on the sheet:
  //   pc
endmodule

module Register_File (
  input  [4:0] RA,
  input  [4:0] RW,
  input  [31:0] BusW,
  input  RegWrite,
  input  [4:0] RB,
  input  in_6,
  output [31:0] BusA,
  output [31:0] BusB
);

  wire IEn0, IEn1, IEn2, IEn3, IEn4, IEn5, IEn6, IEn7, IEn8, IEn9, IEn10, IEn11, IEn12, IEn13, IEn14, IEn15,
       IEn16, IEn17, IEn18, IEn19, IEn20, IEn21, IEn22, IEn23, IEn24, IEn25, IEn26, IEn27, IEn28, IEn29,
       IEn30, IEn31, InputR0, InputR1, InputR2, InputR3, InputR4, InputR5, InputR6, InputR7, InputR8,
       InputR9, InputR10, InputR11, InputR12, InputR13, InputR14, InputR15, InputR16, InputR17, InputR18,
       InputR19, InputR20, InputR21, InputR22, InputR23, InputR24, InputR25, InputR26, InputR27, InputR28,
       InputR29, InputR30, InputR31;
  wire [31:0] DataOut0, DataOut1, DataOut2, DataOut3, DataOut4, DataOut5, DataOut6, DataOut7, DataOut8,
       DataOut9, DataOut10, DataOut11, DataOut12, DataOut13, DataOut14, DataOut15, DataOut16, DataOut17,
       DataOut18, DataOut19, DataOut20, DataOut21, DataOut22, DataOut23, DataOut24, DataOut25, DataOut26,
       DataOut27, DataOut28, DataOut29, DataOut30, DataOut31;

  Decoder #(.select(5), .enable("false")) decoder_1 (
    .out0(InputR0), .out1(InputR1), .out2(InputR2), .out3(InputR3), .out4(InputR4), .out5(InputR5),
    .out6(InputR6), .out7(InputR7), .out8(InputR8), .out9(InputR9), .out10(InputR10), .out11(InputR11),
    .out12(InputR12), .out13(InputR13), .out14(InputR14), .out15(InputR15), .out16(InputR16),
    .out17(InputR17), .out18(InputR18), .out19(InputR19), .out20(InputR20), .out21(InputR21),
    .out22(InputR22), .out23(InputR23), .out24(InputR24), .out25(InputR25), .out26(InputR26),
    .out27(InputR27), .out28(InputR28), .out29(InputR29), .out30(InputR30), .out31(InputR31), .sel(RW));
  and and_1 (IEn0, RegWrite, RegWrite, InputR0, InputR0);
  and and_2 (IEn4, RegWrite, RegWrite, InputR4, InputR4);
  and and_3 (IEn8, RegWrite, RegWrite, InputR8, InputR8);
  and and_4 (IEn12, RegWrite, RegWrite, InputR12, InputR12);
  and and_5 (IEn16, RegWrite, RegWrite, InputR16, InputR16);
  and and_6 (IEn20, RegWrite, RegWrite, InputR20, InputR20);
  and and_7 (IEn24, RegWrite, RegWrite, InputR24, InputR24);
  and and_8 (IEn28, RegWrite, RegWrite, InputR28, InputR28);
  Register #(.width(32)) R0 (.D({32{1'b0}}), .en(IEn0), .Q(DataOut0), .clk(in_6));  // open: clr
  Register #(.width(32)) R4 (.D(BusW), .en(IEn4), .Q(DataOut4), .clk(in_6));  // open: clr
  Register #(.width(32)) R8 (.D(BusW), .en(IEn8), .Q(DataOut8), .clk(in_6));  // open: clr
  Register #(.width(32)) R12 (.D(BusW), .en(IEn12), .Q(DataOut12), .clk(in_6));  // open: clr
  Register #(.width(32)) R16 (.D(BusW), .en(IEn16), .Q(DataOut16), .clk(in_6));  // open: clr
  Register #(.width(32)) R20 (.D(BusW), .en(IEn20), .Q(DataOut20), .clk(in_6));  // open: clr
  Register #(.width(32)) R24 (.D(BusW), .en(IEn24), .Q(DataOut24), .clk(in_6));  // open: clr
  Register #(.width(32)) R28 (.D(BusW), .en(IEn28), .Q(DataOut28), .clk(in_6));  // open: clr
  and and_9 (IEn1, RegWrite, RegWrite, InputR1, InputR1);
  and and_10 (IEn5, RegWrite, RegWrite, InputR5, InputR5);
  and and_11 (IEn9, RegWrite, RegWrite, InputR9, InputR9);
  and and_12 (IEn13, RegWrite, RegWrite, InputR13, InputR13);
  and and_13 (IEn17, RegWrite, RegWrite, InputR17, InputR17);
  and and_14 (IEn21, RegWrite, RegWrite, InputR21, InputR21);
  and and_15 (IEn25, RegWrite, RegWrite, InputR25, InputR25);
  and and_16 (IEn29, RegWrite, RegWrite, InputR29, InputR29);
  Register #(.width(32)) R1 (.D(BusW), .en(IEn1), .Q(DataOut1), .clk(in_6));  // open: clr
  Register #(.width(32)) R5 (.D(BusW), .en(IEn5), .Q(DataOut5), .clk(in_6));  // open: clr
  Register #(.width(32)) R9 (.D(BusW), .en(IEn9), .Q(DataOut9), .clk(in_6));  // open: clr
  Register #(.width(32)) R13 (.D(BusW), .en(IEn13), .Q(DataOut13), .clk(in_6));  // open: clr
  Register #(.width(32)) R17 (.D(BusW), .en(IEn17), .Q(DataOut17), .clk(in_6));  // open: clr
  Register #(.width(32)) R21 (.D(BusW), .en(IEn21), .Q(DataOut21), .clk(in_6));  // open: clr
  Register #(.width(32)) R25 (.D(BusW), .en(IEn25), .Q(DataOut25), .clk(in_6));  // open: clr
  Register #(.width(32)) R29 (.D(BusW), .en(IEn29), .Q(DataOut29), .clk(in_6));  // open: clr
  and and_17 (IEn2, RegWrite, RegWrite, InputR2, InputR2);
  and and_18 (IEn6, RegWrite, RegWrite, InputR6, InputR6);
  and and_19 (IEn10, RegWrite, RegWrite, InputR10, InputR10);
  and and_20 (IEn14, RegWrite, RegWrite, InputR14, InputR14);
  and and_21 (IEn18, RegWrite, RegWrite, InputR18, InputR18);
  and and_22 (IEn22, RegWrite, RegWrite, InputR22, InputR22);
  and and_23 (IEn26, RegWrite, RegWrite, InputR26, InputR26);
  and and_24 (IEn30, RegWrite, RegWrite, InputR30, InputR30);
  Register #(.width(32)) R2 (.D(BusW), .en(IEn2), .Q(DataOut2), .clk(in_6));  // open: clr
  Register #(.width(32)) R6 (.D(BusW), .en(IEn6), .Q(DataOut6), .clk(in_6));  // open: clr
  Register #(.width(32)) R10 (.D(BusW), .en(IEn10), .Q(DataOut10), .clk(in_6));  // open: clr
  Register #(.width(32)) R14 (.D(BusW), .en(IEn14), .Q(DataOut14), .clk(in_6));  // open: clr
  Register #(.width(32)) R18 (.D(BusW), .en(IEn18), .Q(DataOut18), .clk(in_6));  // open: clr
  Register #(.width(32)) R22 (.D(BusW), .en(IEn22), .Q(DataOut22), .clk(in_6));  // open: clr
  Register #(.width(32)) R26 (.D(BusW), .en(IEn26), .Q(DataOut26), .clk(in_6));  // open: clr
  Register #(.width(32)) R30 (.D(BusW), .en(IEn30), .Q(DataOut30), .clk(in_6));  // open: clr
  and and_25 (IEn3, RegWrite, RegWrite, InputR3, InputR3);
  and and_26 (IEn7, RegWrite, RegWrite, InputR7, InputR7);
  and and_27 (IEn11, RegWrite, RegWrite, InputR11, InputR11);
  and and_28 (IEn15, RegWrite, RegWrite, InputR15, InputR15);
  and and_29 (IEn19, RegWrite, RegWrite, InputR19, InputR19);
  and and_30 (IEn23, RegWrite, RegWrite, InputR23, InputR23);
  and and_31 (IEn27, RegWrite, RegWrite, InputR27, InputR27);
  and and_32 (IEn31, RegWrite, RegWrite, InputR31, InputR31);
  Register #(.width(32)) R3 (.D(BusW), .en(IEn3), .Q(DataOut3), .clk(in_6));  // open: clr
  Register #(.width(32)) R7 (.D(BusW), .en(IEn7), .Q(DataOut7), .clk(in_6));  // open: clr
  Register #(.width(32)) R11 (.D(BusW), .en(IEn11), .Q(DataOut11), .clk(in_6));  // open: clr
  Register #(.width(32)) R15 (.D(BusW), .en(IEn15), .Q(DataOut15), .clk(in_6));  // open: clr
  Register #(.width(32)) R19 (.D(BusW), .en(IEn19), .Q(DataOut19), .clk(in_6));  // open: clr
  Register #(.width(32)) R23 (.D(BusW), .en(IEn23), .Q(DataOut23), .clk(in_6));  // open: clr
  Register #(.width(32)) R27 (.D(BusW), .en(IEn27), .Q(DataOut27), .clk(in_6));  // open: clr
  Register #(.width(32)) R31 (.D(BusW), .en(IEn31), .Q(DataOut31), .clk(in_6));  // open: clr
  Multiplexer #(.select(5), .width(32), .enable("false")) multiplexer_1 (
    .in0(DataOut0), .in1(DataOut1), .in2(DataOut2), .in3(DataOut3), .in4(DataOut4), .in5(DataOut5),
    .in6(DataOut6), .in7(DataOut7), .in8(DataOut8), .in9(DataOut9), .in10(DataOut10), .in11(DataOut11),
    .in12(DataOut12), .in13(DataOut13), .in14(DataOut14), .in15(DataOut15), .in16(DataOut16),
    .in17(DataOut17), .in18(DataOut18), .in19(DataOut19), .in20(DataOut20), .in21(DataOut21),
    .in22(DataOut22), .in23(DataOut23), .in24(DataOut24), .in25(DataOut25), .in26(DataOut26),
    .in27(DataOut27), .in28(DataOut28), .in29(DataOut29), .in30(DataOut30), .in31(DataOut31), .out(BusA),
    .sel(RA));
  Multiplexer #(.select(5), .width(32), .enable("false")) multiplexer_2 (
    .in0(DataOut0), .in1(DataOut1), .in2(DataOut2), .in3(DataOut3), .in4(DataOut4), .in5(DataOut5),
    .in6(DataOut6), .in7(DataOut7), .in8(DataOut8), .in9(DataOut9), .in10(DataOut10), .in11(DataOut11),
    .in12(DataOut12), .in13(DataOut13), .in14(DataOut14), .in15(DataOut15), .in16(DataOut16),
    .in17(DataOut17), .in18(DataOut18), .in19(DataOut19), .in20(DataOut20), .in21(DataOut21),
    .in22(DataOut22), .in23(DataOut23), .in24(DataOut24), .in25(DataOut25), .in26(DataOut26),
    .in27(DataOut27), .in28(DataOut28), .in29(DataOut29), .in30(DataOut30), .in31(DataOut31), .out(BusB),
    .sel(RB));

  // Other names for the same wires on the sheet: clck = in_6; DataIn[31:0] = BusW; Write = RegWrite
endmodule
