// Logisim project SBDatapath.circ as structural Verilog: 9 circuits, main circuit main
module main (
  input  [4:0] in_1,
  input  [31:0] in_2
);

  wire ALUBSrc, ALUOp0, ALUOp1, ALUOp2, ALUOp3, ALUOp4, ALUOp5, Branch, Branch_Taken, BranchType0,
       BranchType1, Clck, LSBFlag, MemRead, MemWrite, OverFlowFlag, RegWrite, undriven, ZeroFlag;
  wire [4:0] S1, S2;
  wire [5:0] Opcode;
  wire [15:0] Imm16;
  wire [19:0] Instruction_Address, Next;
  wire [31:0] ALUResult, Imm32, multiplexer_1_out, RA, RB;

  Clock clock_1 (.out(Clck));
  Register #(.width(20), .Select("low")) PC (.D(Next), .en(1'b1), .Q(Instruction_Address), .clk(Clck), .clr(undriven));
  NextPC nextpc_1 (.Extended_Imm(Imm32), .PC(Instruction_Address), .Next_PC(Next), .BranchTaken(Branch_Taken));
  ROM #(.addrWidth(20), .dataWidth(32), .Select("low")) Instruction_Memory (
    .addr(Instruction_Address), .data({Imm16[15:5], S2, S1, Imm16[4:0], Opcode}));
  Register_File register_file_1 (
    .RA(S1), .RB(S2), .in_6(Clck), .BusA(RA), .BusB(RB), .RW(in_1), .RegWrite(RegWrite), .BusW(in_2));
  assign Imm32 = {{16{1'b0}}, Imm16};  // Bit_Extender bit_extender_1
  ControlUnit controlunit_1 (
    .op4(Opcode[4]), .op3(Opcode[3]), .op2(Opcode[2]), .op1(Opcode[1]), .op0(Opcode[0]), .ALUOp5(ALUOp5),
    .ALUOp4(ALUOp4), .ALUOp3(ALUOp3), .ALUOp2(ALUOp2), .ALUOp1(ALUOp1), .ALUOp0(ALUOp0), .Branch(Branch),
    .BranchType1(BranchType1), .BranchType0(BranchType0), .MemWrite(MemWrite), .MemRead(MemRead),
    .RegWrite(RegWrite), .ALUBSourse(ALUBSrc));
  Multiplexer #(.width(32), .enable("false")) multiplexer_1 (
    .in0(Imm32), .in1(RB), .out(multiplexer_1_out), .sel(ALUBSrc));
  ALU alu_1 (
    .in_2(RA), .in_3(multiplexer_1_out), .out_4(ALUResult), .out_5(ZeroFlag), .out_6(OverFlowFlag),
    .out_7(LSBFlag), .in_1({ALUOp5, ALUOp4, ALUOp3, ALUOp2, ALUOp1, ALUOp0}));
  RAM #(.addrWidth(20), .dataWidth(32), .bus("separate"), .simpleMode("false"), .Select("low")) Data_Memory (
    .addr(ALUResult[19:0]), .din(RB), .str(MemWrite), .clk(Clck));  // open: data, sel, ld, clr
  ConditionControl conditioncontrol_1 (
    .Branch(Branch), .BranchType1(BranchType1), .BranchType0(BranchType0), .ZF(ZeroFlag), .LSB(LSBFlag),
    .BranchTaken(Branch_Taken));

  // Other names for the same wires on the sheet: ALUOperationControl[5:0] = {ALUOp5, ALUOp4, ALUOp3, ALUOp2, ALUOp1, ALUOp0};
  //   ImmL[4:0] = Imm16[4:0]; ImmU[10:0] = Imm16[15:5]

  // Notes on the sheet:
  //   contents of Instruction_Memory (hex, n*v repeats v):
  //   208d7
endmodule

module ConditionControl (
  input  Branch,
  input  BranchType1,
  input  BranchType0,
  input  ZF,
  input  LSB,
  output BranchTaken
);

  wire and_1_out, and_2_out, and_3_out, and_4_out, not_1_out, not_2_out, not_3_out, not_4_out, not_5_out,
       not_6_out;

  not not_1 (not_1_out, BranchType1);
  not not_2 (not_2_out, BranchType0);
  not not_3 (not_3_out, BranchType1);
  not not_4 (not_4_out, ZF);
  not not_5 (not_5_out, BranchType0);
  not not_6 (not_6_out, LSB);
  and and_1 (and_1_out, Branch, not_1_out, not_2_out, ZF);
  and and_2 (and_2_out, Branch, not_3_out, BranchType0, not_4_out);
  and and_3 (and_3_out, Branch, BranchType1, not_5_out, LSB);
  and and_4 (and_4_out, Branch, BranchType1, BranchType0, not_6_out);
  or or_1 (BranchTaken, and_1_out, and_2_out, and_3_out, and_4_out);
endmodule

module ControlUnit (
  input  op4,
  input  op3,
  input  op2,
  input  op1,
  input  op0,
  output ALUOp5,
  output ALUOp4,
  output ALUOp3,
  output ALUOp2,
  output ALUOp1,
  output ALUOp0,
  output Branch,
  output BranchType1,
  output BranchType0,
  output MemWrite,
  output MemRead,
  output RegWrite,
  output ALUBSourse
);

  wire not_1_out, not_2_out, not_3_out;

  or or_1 (ALUOp3, op1, op2);
  and and_1 (ALUOp1, op2, op1);
  not not_1 (not_1_out, op1);
  or or_2 (Branch, op1, op2);
  not not_2 (not_2_out, op2);
  not not_3 (not_3_out, op1);
  or or_3 (ALUBSourse, op1, op2);
  and and_2 (ALUOp0, op2, not_1_out);
  and and_3 (MemWrite, not_2_out, not_3_out);

  assign ALUOp2 = 1'b0;
  assign ALUOp4 = 1'b1;
  assign ALUOp5 = op3;
  assign BranchType0 = op0;
  assign BranchType1 = op2;
  assign MemRead = 1'b0;
  assign RegWrite = 1'b0;
endmodule

module NextPC (
  input  [31:0] Extended_Imm,
  input  [19:0] PC,
  input  BranchTaken,
  output [19:0] Next_PC
);

  wire [19:0] adder_2_out, bit_extender_1_out, Target;

  Adder #(.width(20)) adder_1 (.a(Extended_Imm[19:0]), .b(PC), .out(Target));  // open: cin, cout
  assign bit_extender_1_out = {{19{1'b0}}, 1'b1};  // Bit_Extender bit_extender_1
  Adder #(.width(20)) adder_2 (.a(PC), .b(bit_extender_1_out), .out(adder_2_out));  // open: cin, cout
  Multiplexer #(.width(20), .enable("false")) multiplexer_1 (
    .in0(adder_2_out), .in1(Target), .out(Next_PC), .sel(BranchTaken));

  // Other names for the same wires on the sheet: Imm[19:0] = Extended_Imm[19:0]
endmodule

module ALU (
  input  [5:0] in_1,
  input  [31:0] in_2,
  input  [31:0] in_3,
  output [31:0] out_4,
  output out_5,
  output out_6,
  output out_7
);

  wire [31:0] Logic_Result, SET_SSET_Result, Shift_Result;
  wire [31:1] Arth_Result;

  ShifterUnit shifterunit_1 (.in_2(in_2), .in_3(in_3), .out_4(Shift_Result), .OperationControl(in_1[3:0]));
  ArthimeticUnit arthimeticunit_1 (
    .RS1_RD(in_2), .RS2_imm32(in_3), .out_4({Arth_Result, out_7}), .out_5(out_5), .out_6(out_6),
    .OperationControl(in_1[3:0]));
  LogicalUnit logicalunit_1 (.RS1_RD(in_2), .RS2_imm32(in_3), .out_4(Logic_Result), .OperationControl(in_1[3:0]));
  Multiplexer #(.width(32), .enable("false")) multiplexer_1 (
    .in0(in_3), .in1({in_2[15:0], in_3[15:0]}), .out(SET_SSET_Result), .sel(in_1[0]));
  Multiplexer #(.select(2), .width(32), .enable("false")) multiplexer_2 (
    .in0(Shift_Result), .in1({Arth_Result, out_7}), .in2(Logic_Result), .in3(SET_SSET_Result), .out(out_4),
    .sel(in_1[5:4]));

  // Other names for the same wires on the sheet: A[31:0] = in_2; ALU_Operation[5:0] = in_1;
  //   OperationControl[3:0] = in_1[3:0]; ALUResult_Selection[1:0] = in_1[5:4]; Arth_Result[0] = out_7;
  //   overflow = out_6; B[31:0] = in_3; SET[31:0] = in_3; SSET[31:0] = {in_2[15:0], in_3[15:0]}; zero = out_5

  // Notes on the sheet:
  //   Inputs
  //   ALU_OperationContol
  //   Units
  //   Output
endmodule

module LogicalUnit (
  input  [3:0] OperationControl,
  input  [31:0] RS1_RD,
  input  [31:0] RS2_imm32,
  output [31:0] out_4
);

  wire [31:0] AND, NOR, OR, XOR;

  assign AND = RS1_RD & RS2_imm32;  // AND_Gate and_1, 32 bits wide
  assign OR = RS1_RD | RS2_imm32;  // OR_Gate or_1, 32 bits wide
  assign XOR = RS1_RD ^ RS2_imm32;  // XOR_Gate xor_1, 32 bits wide
  assign NOR = ~OR;  // NOT_Gate not_1, 32 bits wide
  Multiplexer #(.select(2), .width(32), .enable("false")) multiplexer_1 (
    .in0(AND), .in1(OR), .in2(NOR), .in3(XOR), .out(out_4), .sel(OperationControl[1:0]));

  // Other names for the same wires on the sheet: A[31:0] = RS1_RD; B[31:0] = RS2_imm32;
  //   Result_Selection[1:0] = OperationControl[1:0]; ArthOp = OperationControl[2]; AluOp_1_bit = OperationControl[3]

  // Notes on the sheet:
  //   Inputs
  //   ADD/SUB_Signal
  //   ArthOpSignal
  //   Operations
  //   Output
endmodule

module ArthimeticUnit (
  input  [3:0] OperationControl,
  input  [31:0] RS1_RD,
  input  [31:0] RS2_imm32,
  output [31:0] out_4,
  output out_5,
  output out_6
);

  wire adder_1_cout, adder_2_cout, comparator_1_lt, xor_2_out;
  wire [31:0] ADD_SUB, ADD_SUB_MUL, bit_extender_1_out, MUL, SEQ, SLT, SLTU, xor_1_out;

  assign xor_1_out = RS2_imm32 ^ bit_extender_1_out;  // XOR_Gate xor_1, 32 bits wide
  assign bit_extender_1_out = {{31{OperationControl[3]}}, OperationControl[3]};  // Bit_Extender bit_extender_1
  Adder #(.width(31)) adder_1 (
    .a(RS1_RD[30:0]), .b(xor_1_out[30:0]), .out(ADD_SUB[30:0]), .cin(OperationControl[3]), .cout(adder_1_cout));
  Adder #(.width(1)) adder_2 (
    .a(RS1_RD[31]), .b(xor_1_out[31]), .out(ADD_SUB[31]), .cin(adder_1_cout), .cout(adder_2_cout));
  xor xor_2 (xor_2_out, ADD_SUB[31], out_6);
  Comparator #(.width(32), .mode("unsigned")) comparator_1 (
    .a(RS1_RD), .b(RS2_imm32), .lt(comparator_1_lt));  // open: gt, eq
  Multiplier #(.width(32)) multiplier_1 (.a(RS1_RD), .b(RS2_imm32), .out(MUL));  // open: cin, cout
  assign SLT = {{31{1'b0}}, xor_2_out};  // Bit_Extender bit_extender_2
  assign SLTU = {{31{1'b0}}, comparator_1_lt};  // Bit_Extender bit_extender_3
  assign SEQ = {{31{1'b0}}, out_5};  // Bit_Extender bit_extender_4
  xor xor_3 (out_6, adder_1_cout, adder_2_cout);
  Multiplexer #(.width(32), .enable("false")) multiplexer_1 (
    .in0(ADD_SUB), .in1(MUL), .out(ADD_SUB_MUL), .sel(OperationControl[2]));
  nor nor_1 (out_5, ADD_SUB[0], ADD_SUB[1], ADD_SUB[2], ADD_SUB[3], ADD_SUB[4], ADD_SUB[5], ADD_SUB[6], ADD_SUB[7], ADD_SUB[8], ADD_SUB[9], ADD_SUB[10], ADD_SUB[11], ADD_SUB[12], ADD_SUB[13], ADD_SUB[14], ADD_SUB[15], ADD_SUB[16], ADD_SUB[17], ADD_SUB[18], ADD_SUB[19], ADD_SUB[20], ADD_SUB[21], ADD_SUB[22], ADD_SUB[23], ADD_SUB[24], ADD_SUB[25], ADD_SUB[26], ADD_SUB[27], ADD_SUB[28], ADD_SUB[29], ADD_SUB[30], ADD_SUB[31]);
  Multiplexer #(.select(2), .width(32)) multiplexer_2 (
    .in0(ADD_SUB_MUL), .in1(SLT), .in2(SLTU), .in3(SEQ), .out(out_4), .sel(OperationControl[1:0]));  // open: en

  // Other names for the same wires on the sheet: A[31:0] = RS1_RD; Sign = ADD_SUB[31]; B[31:0] = RS2_imm32;
  //   Result_Selection[1:0] = OperationControl[1:0]; ArthOp = OperationControl[2]; AluOp_1_bit = OperationControl[3];
  //   Overflow = out_6; Zero = out_5

  // Notes on the sheet:
  //   Inputs
  //   ADD/SUB_Signal
  //   ArthOpSignal
  //   Operations
  //   data out
  //   zero_Detection
  //   outputs
endmodule

module ShifterUnit (
  input  [3:0] OperationControl,
  input  [31:0] in_2,
  input  [31:0] in_3,
  output [31:0] out_4
);

  wire [31:0] Arhimetic_Right, Logical_Left, Logical_Right, Rotate_Right;

  Shifter #(.width(32)) shifter_1 (.in(in_2), .\dist (in_3[4:0]), .out(Logical_Left));
  Shifter #(.width(32), .shift("lr")) shifter_2 (.in(in_2), .\dist (in_3[4:0]), .out(Logical_Right));
  Shifter #(.width(32), .shift("ar")) shifter_3 (.in(in_2), .\dist (in_3[4:0]), .out(Arhimetic_Right));
  Shifter #(.width(32), .shift("rr")) shifter_4 (.in(in_2), .\dist (in_3[4:0]), .out(Rotate_Right));
  Multiplexer #(.select(2), .width(32), .enable("false")) multiplexer_1 (
    .in0(Logical_Left), .in1(Logical_Right), .in2(Arhimetic_Right), .in3(Rotate_Right), .out(out_4),
    .sel(OperationControl[1:0]));

  // Other names for the same wires on the sheet: A[31:0] = in_2; Shift_Amount[4:0] = in_3[4:0];
  //   Result_Selection[1:0] = OperationControl[1:0]; ArthOp = OperationControl[2]; AluOp_1_bit = OperationControl[3]

  // Notes on the sheet:
  //   Inputs
  //   ADD/SUB_Signal
  //   ArthOpSignal
  //   Operations
  //   Output
endmodule

module Register_File (
  input  [4:0] RA,
  input  [4:0] RW,
  input  [31:0] BusW,
  input  RegWrite,
  input  [4:0] RB,
  input  in_6,
  output [31:0] BusA,
  output [31:0] BusB
);

  wire IEn0, IEn1, IEn2, IEn3, IEn4, IEn5, IEn6, IEn7, IEn8, IEn9, IEn10, IEn11, IEn12, IEn13, IEn14, IEn15,
       IEn16, IEn17, IEn18, IEn19, IEn20, IEn21, IEn22, IEn23, IEn24, IEn25, IEn26, IEn27, IEn28, IEn29,
       IEn30, IEn31, InputR0, InputR1, InputR2, InputR3, InputR4, InputR5, InputR6, InputR7, InputR8,
       InputR9, InputR10, InputR11, InputR12, InputR13, InputR14, InputR15, InputR16, InputR17, InputR18,
       InputR19, InputR20, InputR21, InputR22, InputR23, InputR24, InputR25, InputR26, InputR27, InputR28,
       InputR29, InputR30, InputR31;
  wire [31:0] DataOut0, DataOut1, DataOut2, DataOut3, DataOut4, DataOut5, DataOut6, DataOut7, DataOut8,
       DataOut9, DataOut10, DataOut11, DataOut12, DataOut13, DataOut14, DataOut15, DataOut16, DataOut17,
       DataOut18, DataOut19, DataOut20, DataOut21, DataOut22, DataOut23, DataOut24, DataOut25, DataOut26,
       DataOut27, DataOut28, DataOut29, DataOut30, DataOut31;

  Decoder #(.select(5), .enable("false")) decoder_1 (
    .out0(InputR0), .out1(InputR1), .out2(InputR2), .out3(InputR3), .out4(InputR4), .out5(InputR5),
    .out6(InputR6), .out7(InputR7), .out8(InputR8), .out9(InputR9), .out10(InputR10), .out11(InputR11),
    .out12(InputR12), .out13(InputR13), .out14(InputR14), .out15(InputR15), .out16(InputR16),
    .out17(InputR17), .out18(InputR18), .out19(InputR19), .out20(InputR20), .out21(InputR21),
    .out22(InputR22), .out23(InputR23), .out24(InputR24), .out25(InputR25), .out26(InputR26),
    .out27(InputR27), .out28(InputR28), .out29(InputR29), .out30(InputR30), .out31(InputR31), .sel(RW));
  and and_1 (IEn0, RegWrite, InputR0);
  and and_2 (IEn4, RegWrite, InputR4);
  and and_3 (IEn8, RegWrite, InputR8);
  and and_4 (IEn12, RegWrite, InputR12);
  and and_5 (IEn16, RegWrite, InputR16);
  and and_6 (IEn20, RegWrite, InputR20);
  and and_7 (IEn24, RegWrite, InputR24);
  and and_8 (IEn28, RegWrite, InputR28);
  Register #(.width(32), .Select("low")) R0 (.D({32{1'b0}}), .en(IEn0), .Q(DataOut0), .clk(in_6));  // open: clr
  Register #(.width(32), .Select("low")) R4 (.D(BusW), .en(IEn4), .Q(DataOut4), .clk(in_6));  // open: clr
  Register #(.width(32), .Select("low")) R8 (.D(BusW), .en(IEn8), .Q(DataOut8), .clk(in_6));  // open: clr
  Register #(.width(32), .Select("low")) R12 (.D(BusW), .en(IEn12), .Q(DataOut12), .clk(in_6));  // open: clr
  Register #(.width(32), .Select("low")) R16 (.D(BusW), .en(IEn16), .Q(DataOut16), .clk(in_6));  // open: clr
  Register #(.width(32), .Select("low")) R20 (.D(BusW), .en(IEn20), .Q(DataOut20), .clk(in_6));  // open: clr
  Register #(.width(32), .Select("low")) R24 (.D(BusW), .en(IEn24), .Q(DataOut24), .clk(in_6));  // open: clr
  Register #(.width(32), .Select("low")) R28 (.D(BusW), .en(IEn28), .Q(DataOut28), .clk(in_6));  // open: clr
  and and_9 (IEn1, RegWrite, InputR1);
  and and_10 (IEn5, RegWrite, InputR5);
  and and_11 (IEn9, RegWrite, InputR9);
  and and_12 (IEn13, RegWrite, InputR13);
  and and_13 (IEn17, RegWrite, InputR17);
  and and_14 (IEn21, RegWrite, InputR21);
  and and_15 (IEn25, RegWrite, InputR25);
  and and_16 (IEn29, RegWrite, InputR29);
  Register #(.width(32), .Select("low")) R1 (.D(BusW), .en(IEn1), .Q(DataOut1), .clk(in_6));  // open: clr
  Register #(.width(32), .Select("low")) R5 (.D(BusW), .en(IEn5), .Q(DataOut5), .clk(in_6));  // open: clr
  Register #(.width(32), .Select("low")) R9 (.D(BusW), .en(IEn9), .Q(DataOut9), .clk(in_6));  // open: clr
  Register #(.width(32), .Select("low")) R13 (.D(BusW), .en(IEn13), .Q(DataOut13), .clk(in_6));  // open: clr
  Register #(.width(32), .Select("low")) R17 (.D(BusW), .en(IEn17), .Q(DataOut17), .clk(in_6));  // open: clr
  Register #(.width(32), .Select("low")) R21 (.D(BusW), .en(IEn21), .Q(DataOut21), .clk(in_6));  // open: clr
  Register #(.width(32), .Select("low")) R25 (.D(BusW), .en(IEn25), .Q(DataOut25), .clk(in_6));  // open: clr
  Register #(.width(32), .Select("low")) R29 (.D(BusW), .en(IEn29), .Q(DataOut29), .clk(in_6));  // open: clr
  and and_17 (IEn2, RegWrite, InputR2);
  and and_18 (IEn6, RegWrite, InputR6);
  and and_19 (IEn10, RegWrite, InputR10);
  and and_20 (IEn14, RegWrite, InputR14);
  and and_21 (IEn18, RegWrite, InputR18);
  and and_22 (IEn22, RegWrite, InputR22);
  and and_23 (IEn26, RegWrite, InputR26);
  and and_24 (IEn30, RegWrite, InputR30);
  Register #(.width(32), .Select("low")) R2 (.D(BusW), .en(IEn2), .Q(DataOut2), .clk(in_6));  // open: clr
  Register #(.width(32), .Select("low")) R6 (.D(BusW), .en(IEn6), .Q(DataOut6), .clk(in_6));  // open: clr
  Register #(.width(32), .Select("low")) R10 (.D(BusW), .en(IEn10), .Q(DataOut10), .clk(in_6));  // open: clr
  Register #(.width(32), .Select("low")) R14 (.D(BusW), .en(IEn14), .Q(DataOut14), .clk(in_6));  // open: clr
  Register #(.width(32), .Select("low")) R18 (.D(BusW), .en(IEn18), .Q(DataOut18), .clk(in_6));  // open: clr
  Register #(.width(32), .Select("low")) R22 (.D(BusW), .en(IEn22), .Q(DataOut22), .clk(in_6));  // open: clr
  Register #(.width(32), .Select("low")) R26 (.D(BusW), .en(IEn26), .Q(DataOut26), .clk(in_6));  // open: clr
  Register #(.width(32), .Select("low")) R30 (.D(BusW), .en(IEn30), .Q(DataOut30), .clk(in_6));  // open: clr
  and and_25 (IEn3, RegWrite, InputR3);
  and and_26 (IEn7, RegWrite, InputR7);
  and and_27 (IEn11, RegWrite, InputR11);
  and and_28 (IEn15, RegWrite, InputR15);
  and and_29 (IEn19, RegWrite, InputR19);
  and and_30 (IEn23, RegWrite, InputR23);
  and and_31 (IEn27, RegWrite, InputR27);
  and and_32 (IEn31, RegWrite, InputR31);
  Register #(.width(32), .Select("low")) R3 (.D(BusW), .en(IEn3), .Q(DataOut3), .clk(in_6));  // open: clr
  Register #(.width(32), .Select("low")) R7 (.D(BusW), .en(IEn7), .Q(DataOut7), .clk(in_6));  // open: clr
  Register #(.width(32), .Select("low")) R11 (.D(BusW), .en(IEn11), .Q(DataOut11), .clk(in_6));  // open: clr
  Register #(.width(32), .Select("low")) R15 (.D(BusW), .en(IEn15), .Q(DataOut15), .clk(in_6));  // open: clr
  Register #(.width(32), .Select("low")) R19 (.D(BusW), .en(IEn19), .Q(DataOut19), .clk(in_6));  // open: clr
  Register #(.width(32), .Select("low")) R23 (.D(BusW), .en(IEn23), .Q(DataOut23), .clk(in_6));  // open: clr
  Register #(.width(32), .Select("low")) R27 (.D(BusW), .en(IEn27), .Q(DataOut27), .clk(in_6));  // open: clr
  Register #(.width(32), .Select("low")) R31 (.D(BusW), .en(IEn31), .Q(DataOut31), .clk(in_6));  // open: clr
  Multiplexer #(.select(5), .width(32), .enable("false")) multiplexer_1 (
    .in0(DataOut0), .in1(DataOut1), .in2(DataOut2), .in3(DataOut3), .in4(DataOut4), .in5(DataOut5),
    .in6(DataOut6), .in7(DataOut7), .in8(DataOut8), .in9(DataOut9), .in10(DataOut10), .in11(DataOut11),
    .in12(DataOut12), .in13(DataOut13), .in14(DataOut14), .in15(DataOut15), .in16(DataOut16),
    .in17(DataOut17), .in18(DataOut18), .in19(DataOut19), .in20(DataOut20), .in21(DataOut21),
    .in22(DataOut22), .in23(DataOut23), .in24(DataOut24), .in25(DataOut25), .in26(DataOut26),
    .in27(DataOut27), .in28(DataOut28), .in29(DataOut29), .in30(DataOut30), .in31(DataOut31), .out(BusA),
    .sel(RA));
  Multiplexer #(.select(5), .width(32), .enable("false")) multiplexer_2 (
    .in0(DataOut0), .in1(DataOut1), .in2(DataOut2), .in3(DataOut3), .in4(DataOut4), .in5(DataOut5),
    .in6(DataOut6), .in7(DataOut7), .in8(DataOut8), .in9(DataOut9), .in10(DataOut10), .in11(DataOut11),
    .in12(DataOut12), .in13(DataOut13), .in14(DataOut14), .in15(DataOut15), .in16(DataOut16),
    .in17(DataOut17), .in18(DataOut18), .in19(DataOut19), .in20(DataOut20), .in21(DataOut21),
    .in22(DataOut22), .in23(DataOut23), .in24(DataOut24), .in25(DataOut25), .in26(DataOut26),
    .in27(DataOut27), .in28(DataOut28), .in29(DataOut29), .in30(DataOut30), .in31(DataOut31), .out(BusB),
    .sel(RB));

  // Other names for the same wires on the sheet: clck = in_6; DataIn[31:0] = BusW; Write = RegWrite
endmodule
