// Logisim project Data_Path_with_test_registers.circ as structural Verilog
module Data_path (
);

  wire B_Alu_Slc, B_taken, branch, clk, imm_select_1_imm_slc, Jump, LSB, OverFlow, ReadSignal, RegWr,
       SignSlc, SourceSlc, undriven, WriteSgnal, ZeroFlag;
  wire [1:0] B_TYPE, WBSlc;
  wire [4:0] d, imm16, multiplexer_1_out, S1;
  wire [5:0] ALUOpCtrl, OP;
  wire [10:0] Func;
  wire [19:0] adder_1_out, Next_PC, PC;
  wire [31:0] A, AluResult, B, bit_extender_2_out, imm32, Imm32_U_L, multiplexer_2_out, multiplexer_3_out,
       R0, R1, R2, R3, R4, R5, R6, R7, R8, R9, R10, R11, R12, R13, R14, R15, R16, R17, R18, R19, R20, R21,
       R22, R23, R24, R25, R26, R27, R28, R29, R30, R31, ram_1_data, WB;

  PCNEXT pcnext_1 (.in_1(Imm32_U_L), .in_2(PC), .in_3(AluResult[19:0]), .in_4(Jump), .out_6(Next_PC), .in_5(B_taken));
  Branch_Ctrl branch_ctrl_1 (
    .Branch(branch), .BranchType1(B_TYPE[1]), .BranchType0(B_TYPE[0]), .ZF(ZeroFlag), .LSB(LSB),
    .BranchTaken(B_taken));
  Register #(.width(20)) u_PC (.D(Next_PC), .Q(PC), .clk(clk), .clr(undriven));  // open: en
  Clock clock_1 (.out(clk));
  extender extender_1 (.in_1({Func, imm16}), .out_3(imm32), .in_2(SignSlc));
  ROM #(.addrWidth(20), .dataWidth(32)) rom_1 (.addr(PC), .data({Func, imm16, S1, d, OP}));  // open: sel
  assign Imm32_U_L = {{16{Func[10]}}, {Func, d}};  // Bit_Extender bit_extender_1
  MainControlUnit maincontrolunit_1 (
    .jump(Jump), .branch(branch), .SignSlc(SignSlc), .SourceSlc(SourceSlc), .RegWr(RegWr),
    .B_Alu_slc(B_Alu_Slc), .WrMemory(WriteSgnal), .ReadMemory(ReadSignal), .in_1(OP), .B_TYPE(B_TYPE),
    .WB_SLC(WBSlc));
  Multiplexer #(.width(5), .enable("false")) multiplexer_1 (
    .in0(S1), .in1(d), .out(multiplexer_1_out), .sel(SourceSlc));
  ALUOperation aluoperation_1 (.in_1(OP), .in_2(Func), .out_3(ALUOpCtrl));
  Reg_File_Test reg_file_test_1 (
    .RA(multiplexer_1_out), .RB(imm16), .in_6(clk), .BusA(A), .BusB(B), .out_8(R16), .out_9(R15),
    .out_10(R14), .out_11(R13), .out_12(R12), .out_13(R11), .out_14(R10), .out_15(R9), .out_16(R8),
    .out_17(R7), .out_18(R6), .out_19(R5), .out_20(R4), .out_21(R3), .out_22(R2), .out_23(R1), .out_7(R0),
    .RW(d), .RegWrite(RegWr), .BusW(WB), .out_26(R31), .out_27(R30), .out_28(R29), .out_29(R28),
    .out_30(R27), .out_31(R26), .out_32(R25), .out_33(R24), .out_34(R23), .out_35(R22), .out_36(R21),
    .out_37(R20), .out_38(R19), .out_39(R18), .out_40(R17));
  // Probe on R15
  // Probe on R31
  // Probe on R14
  // Probe on R30
  Imm_select imm_select_1 (.in_1(OP), .imm_slc(imm_select_1_imm_slc));
  // Probe on R13
  // Probe on R29
  Multiplexer #(.width(32), .enable("false")) multiplexer_2 (
    .in0(Imm32_U_L), .in1(imm32), .out(multiplexer_2_out), .sel(imm_select_1_imm_slc));
  // Probe on R12
  // Probe on R28
  Multiplexer #(.width(32), .enable("false")) multiplexer_3 (
    .in0(multiplexer_2_out), .in1(B), .out(multiplexer_3_out), .sel(B_Alu_Slc));
  // Probe on R11
  // Probe on R27
  // Probe on R10
  // Probe on R26
  // Probe on R9
  // Probe on R25
  ALU_Unit alu_unit_1 (
    .in_2(A), .in_3(multiplexer_3_out), .out_4(AluResult), .out_5(ZeroFlag), .out_6(OverFlow), .out_7(LSB),
    .in_1(ALUOpCtrl));
  // Probe on R8
  // Probe on R24
  // Probe on R7
  // Probe on R23
  // Probe on R6
  // Probe on R22
  // Probe on R5
  // Probe on R21
  RAM #(.addrWidth(20), .dataWidth(32), .bus("separate")) ram_1 (
    .addr(AluResult[19:0]), .din(B), .data(ram_1_data), .str(WriteSgnal), .clk(clk), .ld(ReadSignal));  // open: sel, clr
  // Probe on R4
  // Probe on R20
  Adder #(.width(20)) adder_1 (.a(PC), .b(20'h1), .out(adder_1_out));  // open: cin, cout
  // Probe on R3
  // Probe on R19
  assign bit_extender_2_out = {{12{1'b0}}, adder_1_out};  // Bit_Extender bit_extender_2
  // Probe on R2
  // Probe on R18
  Multiplexer #(.select(2), .width(32), .enable("false")) multiplexer_4 (
    .in0(AluResult), .in1(ram_1_data), .in2(bit_extender_2_out), .out(WB), .sel(WBSlc));  // open: in3
  // Probe on R1
  // Probe on R17
  // Probe on R0
  // Probe on R16

  // Other names for the same wires on the sheet: S2[4:0] = imm16; Sa[4:0] = imm16; immL[4:0] = d; imm16[15:5] = Func;
  //   immU[10:0] = Func

  // Notes on the sheet:
  //   IM
  //   contents of rom_1 (hex, n*v repeats v):
  //   384004d 1234020d 5678020e 140945 12508c0 834100 50 10090 200d0 a42100 841100 c31180 30d2 820880
  //   ffe00712 40011 1a31280 245380 4453c0 57684 1a01cf 4545024d 4545028d 95095 ffff0dcb 12 1431140 50
  //   50890 608d0 1631100 40011 380f
  //   Registers Output
  //   DM
  //   writebackSlc
endmodule

module PCNEXT (
  input  [31:0] in_1,
  input  [19:0] in_2,
  input  [19:0] in_3,
  input  in_4,
  input  in_5,
  output [19:0] out_6
);

  wire [19:0] pc_next_sbtype_1_next_pc;

  PC_NEXT_SBTYPE pc_next_sbtype_1 (
    .Extended_Imm(in_1), .PC(in_2), .Next_PC(pc_next_sbtype_1_next_pc), .BranchTaken(in_5));
  Multiplexer #(.width(20), .enable("false")) multiplexer_1 (
    .in0(pc_next_sbtype_1_next_pc), .in1(in_3), .out(out_6), .sel(in_4));
endmodule

module PC_NEXT_SBTYPE (
  input  [31:0] Extended_Imm,
  input  [19:0] PC,
  input  BranchTaken,
  output [19:0] Next_PC
);

  wire [19:0] adder_2_out, bit_extender_1_out, Target;

  Adder #(.width(20)) adder_1 (.a(Extended_Imm[19:0]), .b(PC), .out(Target));  // open: cin, cout
  assign bit_extender_1_out = {{19{1'b0}}, 1'b1};  // Bit_Extender bit_extender_1
  Adder #(.width(20)) adder_2 (.a(PC), .b(bit_extender_1_out), .out(adder_2_out));  // open: cin, cout
  Multiplexer #(.width(20), .enable("false")) multiplexer_1 (
    .in0(adder_2_out), .in1(Target), .out(Next_PC), .sel(BranchTaken));

  // Other names for the same wires on the sheet: Imm[19:0] = Extended_Imm[19:0]
endmodule

module Branch_Ctrl (
  input  Branch,
  input  BranchType1,
  input  BranchType0,
  input  ZF,
  input  LSB,
  output BranchTaken
);

  wire and_1_out, and_2_out, and_3_out, and_4_out, not_1_out, not_2_out, not_3_out, not_4_out, not_5_out,
       not_6_out;

  not not_1 (not_1_out, BranchType1);
  not not_2 (not_2_out, BranchType0);
  not not_3 (not_3_out, BranchType1);
  not not_4 (not_4_out, ZF);
  not not_5 (not_5_out, BranchType0);
  not not_6 (not_6_out, LSB);
  and and_1 (and_1_out, Branch, not_1_out, not_2_out, ZF);
  and and_2 (and_2_out, Branch, not_3_out, BranchType0, not_4_out);
  and and_3 (and_3_out, Branch, BranchType1, not_5_out, LSB);
  and and_4 (and_4_out, Branch, BranchType1, BranchType0, not_6_out);
  or or_1 (BranchTaken, and_1_out, and_2_out, and_3_out, and_4_out);
endmodule

module Register_File (
  input  [4:0] RA,
  input  [4:0] RW,
  input  [31:0] BusW,
  input  RegWrite,
  input  [4:0] RB,
  input  in_6,
  output [31:0] BusA,
  output [31:0] BusB
);

  wire IEn0, IEn1, IEn2, IEn3, IEn4, IEn5, IEn6, IEn7, IEn8, IEn9, IEn10, IEn11, IEn12, IEn13, IEn14, IEn15,
       IEn16, IEn17, IEn18, IEn19, IEn20, IEn21, IEn22, IEn23, IEn24, IEn25, IEn26, IEn27, IEn28, IEn29,
       IEn30, IEn31, InputR0, InputR1, InputR2, InputR3, InputR4, InputR5, InputR6, InputR7, InputR8,
       InputR9, InputR10, InputR11, InputR12, InputR13, InputR14, InputR15, InputR16, InputR17, InputR18,
       InputR19, InputR20, InputR21, InputR22, InputR23, InputR24, InputR25, InputR26, InputR27, InputR28,
       InputR29, InputR30, InputR31;
  wire [31:0] DataOut0, DataOut1, DataOut2, DataOut3, DataOut4, DataOut5, DataOut6, DataOut7, DataOut8,
       DataOut9, DataOut10, DataOut11, DataOut12, DataOut13, DataOut14, DataOut15, DataOut16, DataOut17,
       DataOut18, DataOut19, DataOut20, DataOut21, DataOut22, DataOut23, DataOut24, DataOut25, DataOut26,
       DataOut27, DataOut28, DataOut29, DataOut30, DataOut31;

  Decoder #(.select(5), .enable("false")) decoder_1 (
    .out0(InputR0), .out1(InputR1), .out2(InputR2), .out3(InputR3), .out4(InputR4), .out5(InputR5),
    .out6(InputR6), .out7(InputR7), .out8(InputR8), .out9(InputR9), .out10(InputR10), .out11(InputR11),
    .out12(InputR12), .out13(InputR13), .out14(InputR14), .out15(InputR15), .out16(InputR16),
    .out17(InputR17), .out18(InputR18), .out19(InputR19), .out20(InputR20), .out21(InputR21),
    .out22(InputR22), .out23(InputR23), .out24(InputR24), .out25(InputR25), .out26(InputR26),
    .out27(InputR27), .out28(InputR28), .out29(InputR29), .out30(InputR30), .out31(InputR31), .sel(RW));
  and and_1 (IEn0, RegWrite, RegWrite, InputR0, InputR0);
  and and_2 (IEn4, RegWrite, RegWrite, InputR4, InputR4);
  and and_3 (IEn8, RegWrite, RegWrite, InputR8, InputR8);
  and and_4 (IEn12, RegWrite, RegWrite, InputR12, InputR12);
  and and_5 (IEn16, RegWrite, RegWrite, InputR16, InputR16);
  and and_6 (IEn20, RegWrite, RegWrite, InputR20, InputR20);
  and and_7 (IEn24, RegWrite, RegWrite, InputR24, InputR24);
  and and_8 (IEn28, RegWrite, RegWrite, InputR28, InputR28);
  Register #(.width(32)) R0 (.D({32{1'b0}}), .en(IEn0), .Q(DataOut0), .clk(in_6));  // open: clr
  Register #(.width(32)) R4 (.D(BusW), .en(IEn4), .Q(DataOut4), .clk(in_6));  // open: clr
  Register #(.width(32)) R8 (.D(BusW), .en(IEn8), .Q(DataOut8), .clk(in_6));  // open: clr
  Register #(.width(32)) R12 (.D(BusW), .en(IEn12), .Q(DataOut12), .clk(in_6));  // open: clr
  Register #(.width(32)) R16 (.D(BusW), .en(IEn16), .Q(DataOut16), .clk(in_6));  // open: clr
  Register #(.width(32)) R20 (.D(BusW), .en(IEn20), .Q(DataOut20), .clk(in_6));  // open: clr
  Register #(.width(32)) R24 (.D(BusW), .en(IEn24), .Q(DataOut24), .clk(in_6));  // open: clr
  Register #(.width(32)) R28 (.D(BusW), .en(IEn28), .Q(DataOut28), .clk(in_6));  // open: clr
  and and_9 (IEn1, RegWrite, RegWrite, InputR1, InputR1);
  and and_10 (IEn5, RegWrite, RegWrite, InputR5, InputR5);
  and and_11 (IEn9, RegWrite, RegWrite, InputR9, InputR9);
  and and_12 (IEn13, RegWrite, RegWrite, InputR13, InputR13);
  and and_13 (IEn17, RegWrite, RegWrite, InputR17, InputR17);
  and and_14 (IEn21, RegWrite, RegWrite, InputR21, InputR21);
  and and_15 (IEn25, RegWrite, RegWrite, InputR25, InputR25);
  and and_16 (IEn29, RegWrite, RegWrite, InputR29, InputR29);
  Register #(.width(32)) R1 (.D(BusW), .en(IEn1), .Q(DataOut1), .clk(in_6));  // open: clr
  Register #(.width(32)) R5 (.D(BusW), .en(IEn5), .Q(DataOut5), .clk(in_6));  // open: clr
  Register #(.width(32)) R9 (.D(BusW), .en(IEn9), .Q(DataOut9), .clk(in_6));  // open: clr
  Register #(.width(32)) R13 (.D(BusW), .en(IEn13), .Q(DataOut13), .clk(in_6));  // open: clr
  Register #(.width(32)) R17 (.D(BusW), .en(IEn17), .Q(DataOut17), .clk(in_6));  // open: clr
  Register #(.width(32)) R21 (.D(BusW), .en(IEn21), .Q(DataOut21), .clk(in_6));  // open: clr
  Register #(.width(32)) R25 (.D(BusW), .en(IEn25), .Q(DataOut25), .clk(in_6));  // open: clr
  Register #(.width(32)) R29 (.D(BusW), .en(IEn29), .Q(DataOut29), .clk(in_6));  // open: clr
  and and_17 (IEn2, RegWrite, RegWrite, InputR2, InputR2);
  and and_18 (IEn6, RegWrite, RegWrite, InputR6, InputR6);
  and and_19 (IEn10, RegWrite, RegWrite, InputR10, InputR10);
  and and_20 (IEn14, RegWrite, RegWrite, InputR14, InputR14);
  and and_21 (IEn18, RegWrite, RegWrite, InputR18, InputR18);
  and and_22 (IEn22, RegWrite, RegWrite, InputR22, InputR22);
  and and_23 (IEn26, RegWrite, RegWrite, InputR26, InputR26);
  and and_24 (IEn30, RegWrite, RegWrite, InputR30, InputR30);
  Register #(.width(32)) R2 (.D(BusW), .en(IEn2), .Q(DataOut2), .clk(in_6));  // open: clr
  Register #(.width(32)) R6 (.D(BusW), .en(IEn6), .Q(DataOut6), .clk(in_6));  // open: clr
  Register #(.width(32)) R10 (.D(BusW), .en(IEn10), .Q(DataOut10), .clk(in_6));  // open: clr
  Register #(.width(32)) R14 (.D(BusW), .en(IEn14), .Q(DataOut14), .clk(in_6));  // open: clr
  Register #(.width(32)) R18 (.D(BusW), .en(IEn18), .Q(DataOut18), .clk(in_6));  // open: clr
  Register #(.width(32)) R22 (.D(BusW), .en(IEn22), .Q(DataOut22), .clk(in_6));  // open: clr
  Register #(.width(32)) R26 (.D(BusW), .en(IEn26), .Q(DataOut26), .clk(in_6));  // open: clr
  Register #(.width(32)) R30 (.D(BusW), .en(IEn30), .Q(DataOut30), .clk(in_6));  // open: clr
  and and_25 (IEn3, RegWrite, RegWrite, InputR3, InputR3);
  and and_26 (IEn7, RegWrite, RegWrite, InputR7, InputR7);
  and and_27 (IEn11, RegWrite, RegWrite, InputR11, InputR11);
  and and_28 (IEn15, RegWrite, RegWrite, InputR15, InputR15);
  and and_29 (IEn19, RegWrite, RegWrite, InputR19, InputR19);
  and and_30 (IEn23, RegWrite, RegWrite, InputR23, InputR23);
  and and_31 (IEn27, RegWrite, RegWrite, InputR27, InputR27);
  and and_32 (IEn31, RegWrite, RegWrite, InputR31, InputR31);
  Register #(.width(32)) R3 (.D(BusW), .en(IEn3), .Q(DataOut3), .clk(in_6));  // open: clr
  Register #(.width(32)) R7 (.D(BusW), .en(IEn7), .Q(DataOut7), .clk(in_6));  // open: clr
  Register #(.width(32)) R11 (.D(BusW), .en(IEn11), .Q(DataOut11), .clk(in_6));  // open: clr
  Register #(.width(32)) R15 (.D(BusW), .en(IEn15), .Q(DataOut15), .clk(in_6));  // open: clr
  Register #(.width(32)) R19 (.D(BusW), .en(IEn19), .Q(DataOut19), .clk(in_6));  // open: clr
  Register #(.width(32)) R23 (.D(BusW), .en(IEn23), .Q(DataOut23), .clk(in_6));  // open: clr
  Register #(.width(32)) R27 (.D(BusW), .en(IEn27), .Q(DataOut27), .clk(in_6));  // open: clr
  Register #(.width(32)) R31 (.D(BusW), .en(IEn31), .Q(DataOut31), .clk(in_6));  // open: clr
  Multiplexer #(.select(5), .width(32), .enable("false")) multiplexer_1 (
    .in0(DataOut0), .in1(DataOut1), .in2(DataOut2), .in3(DataOut3), .in4(DataOut4), .in5(DataOut5),
    .in6(DataOut6), .in7(DataOut7), .in8(DataOut8), .in9(DataOut9), .in10(DataOut10), .in11(DataOut11),
    .in12(DataOut12), .in13(DataOut13), .in14(DataOut14), .in15(DataOut15), .in16(DataOut16),
    .in17(DataOut17), .in18(DataOut18), .in19(DataOut19), .in20(DataOut20), .in21(DataOut21),
    .in22(DataOut22), .in23(DataOut23), .in24(DataOut24), .in25(DataOut25), .in26(DataOut26),
    .in27(DataOut27), .in28(DataOut28), .in29(DataOut29), .in30(DataOut30), .in31(DataOut31), .out(BusA),
    .sel(RA));
  Multiplexer #(.select(5), .width(32), .enable("false")) multiplexer_2 (
    .in0(DataOut0), .in1(DataOut1), .in2(DataOut2), .in3(DataOut3), .in4(DataOut4), .in5(DataOut5),
    .in6(DataOut6), .in7(DataOut7), .in8(DataOut8), .in9(DataOut9), .in10(DataOut10), .in11(DataOut11),
    .in12(DataOut12), .in13(DataOut13), .in14(DataOut14), .in15(DataOut15), .in16(DataOut16),
    .in17(DataOut17), .in18(DataOut18), .in19(DataOut19), .in20(DataOut20), .in21(DataOut21),
    .in22(DataOut22), .in23(DataOut23), .in24(DataOut24), .in25(DataOut25), .in26(DataOut26),
    .in27(DataOut27), .in28(DataOut28), .in29(DataOut29), .in30(DataOut30), .in31(DataOut31), .out(BusB),
    .sel(RB));

  // Other names for the same wires on the sheet: clck = in_6; DataIn[31:0] = BusW; Write = RegWrite
endmodule

module ALU_Unit (
  input  [5:0] in_1,
  input  [31:0] in_2,
  input  [31:0] in_3,
  output [31:0] out_4,
  output out_5,
  output out_6,
  output out_7
);

  wire [31:0] Logic_Result, SET_SSET_Result, Shift_Result;
  wire [31:1] Arth_Result;

  ShiftUnit shiftunit_1 (.in_2(in_2), .in_3(in_3), .out_4(Shift_Result), .OperationControl(in_1[3:0]));
  ArithmeticUnit arithmeticunit_1 (
    .RS1_RD(in_2), .RS2_imm32(in_3), .out_4({Arth_Result, out_7}), .out_5(out_5), .out_6(out_6),
    .OperationControl(in_1[3:0]));
  LogicalUnit logicalunit_1 (.RS1_RD(in_2), .RS2_imm32(in_3), .out_4(Logic_Result), .OperationControl(in_1[3:0]));
  Multiplexer #(.width(32), .enable("false")) multiplexer_1 (
    .in0(in_3), .in1({in_2[15:0], in_3[15:0]}), .out(SET_SSET_Result), .sel(in_1[0]));
  Multiplexer #(.select(2), .width(32), .enable("false")) multiplexer_2 (
    .in0(Shift_Result), .in1({Arth_Result, out_7}), .in2(Logic_Result), .in3(SET_SSET_Result), .out(out_4),
    .sel(in_1[5:4]));

  // Other names for the same wires on the sheet: A[31:0] = in_2; ALU_Operation[5:0] = in_1;
  //   OperationControl[3:0] = in_1[3:0]; ALUResult_Selection[1:0] = in_1[5:4]; Arth_Result[0] = out_7;
  //   overflow = out_6; B[31:0] = in_3; SET[31:0] = in_3; SSET[31:0] = {in_2[15:0], in_3[15:0]}; zero = out_5

  // Notes on the sheet:
  //   Inputs
  //   ALU_OperationContol
  //   Units
  //   Output
endmodule

module ShiftUnit (
  input  [3:0] OperationControl,
  input  [31:0] in_2,
  input  [31:0] in_3,
  output [31:0] out_4
);

  wire [31:0] Arhimetic_Right, Logical_Left, Logical_Right, Rotate_Right;

  Shifter #(.width(32)) shifter_1 (.in(in_2), .\dist (in_3[4:0]), .out(Logical_Left));
  Shifter #(.width(32), .shift("lr")) shifter_2 (.in(in_2), .\dist (in_3[4:0]), .out(Logical_Right));
  Shifter #(.width(32), .shift("ar")) shifter_3 (.in(in_2), .\dist (in_3[4:0]), .out(Arhimetic_Right));
  Shifter #(.width(32), .shift("rr")) shifter_4 (.in(in_2), .\dist (in_3[4:0]), .out(Rotate_Right));
  Multiplexer #(.select(2), .width(32), .enable("false")) multiplexer_1 (
    .in0(Logical_Left), .in1(Logical_Right), .in2(Arhimetic_Right), .in3(Rotate_Right), .out(out_4),
    .sel(OperationControl[1:0]));

  // Other names for the same wires on the sheet: A[31:0] = in_2; Shift_Amount[4:0] = in_3[4:0];
  //   Result_Selection[1:0] = OperationControl[1:0]; ArthOp = OperationControl[2]; AluOp_1_bit = OperationControl[3]

  // Notes on the sheet:
  //   Inputs
  //   ADD/SUB_Signal
  //   ArthOpSignal
  //   Operations
  //   Output
endmodule

module ArithmeticUnit (
  input  [3:0] OperationControl,
  input  [31:0] RS1_RD,
  input  [31:0] RS2_imm32,
  output [31:0] out_4,
  output out_5,
  output out_6
);

  wire adder_1_cout, adder_2_cout, comparator_1_lt, xor_2_out;
  wire [31:0] ADD_SUB, ADD_SUB_MUL, bit_extender_1_out, MUL, SEQ, SLT, SLTU, xor_1_out;

  assign xor_1_out = RS2_imm32 ^ bit_extender_1_out;  // XOR_Gate xor_1, 32 bits wide
  assign bit_extender_1_out = {{31{OperationControl[3]}}, OperationControl[3]};  // Bit_Extender bit_extender_1
  Adder #(.width(31)) adder_1 (
    .a(RS1_RD[30:0]), .b(xor_1_out[30:0]), .out(ADD_SUB[30:0]), .cin(OperationControl[3]), .cout(adder_1_cout));
  Adder #(.width(1)) adder_2 (
    .a(RS1_RD[31]), .b(xor_1_out[31]), .out(ADD_SUB[31]), .cin(adder_1_cout), .cout(adder_2_cout));
  xor xor_2 (xor_2_out, ADD_SUB[31], out_6);
  Comparator #(.width(32), .mode("unsigned")) comparator_1 (
    .a(RS1_RD), .b(RS2_imm32), .lt(comparator_1_lt));  // open: gt, eq
  Multiplier #(.width(32)) multiplier_1 (.a(RS1_RD), .b(RS2_imm32), .out(MUL));  // open: cin, cout
  assign SLT = {{31{1'b0}}, xor_2_out};  // Bit_Extender bit_extender_2
  assign SLTU = {{31{1'b0}}, comparator_1_lt};  // Bit_Extender bit_extender_3
  assign SEQ = {{31{1'b0}}, out_5};  // Bit_Extender bit_extender_4
  xor xor_3 (out_6, adder_1_cout, adder_2_cout);
  Multiplexer #(.width(32), .enable("false")) multiplexer_1 (
    .in0(ADD_SUB), .in1(MUL), .out(ADD_SUB_MUL), .sel(OperationControl[2]));
  nor nor_1 (out_5, ADD_SUB[0], ADD_SUB[1], ADD_SUB[2], ADD_SUB[3], ADD_SUB[4], ADD_SUB[5], ADD_SUB[6], ADD_SUB[7], ADD_SUB[8], ADD_SUB[9], ADD_SUB[10], ADD_SUB[11], ADD_SUB[12], ADD_SUB[13], ADD_SUB[14], ADD_SUB[15], ADD_SUB[16], ADD_SUB[17], ADD_SUB[18], ADD_SUB[19], ADD_SUB[20], ADD_SUB[21], ADD_SUB[22], ADD_SUB[23], ADD_SUB[24], ADD_SUB[25], ADD_SUB[26], ADD_SUB[27], ADD_SUB[28], ADD_SUB[29], ADD_SUB[30], ADD_SUB[31]);
  Multiplexer #(.select(2), .width(32)) multiplexer_2 (
    .in0(ADD_SUB_MUL), .in1(SLT), .in2(SLTU), .in3(SEQ), .out(out_4), .sel(OperationControl[1:0]));  // open: en

  // Other names for the same wires on the sheet: A[31:0] = RS1_RD; Sign = ADD_SUB[31]; B[31:0] = RS2_imm32;
  //   Result_Selection[1:0] = OperationControl[1:0]; ArthOp = OperationControl[2]; AluOp_1_bit = OperationControl[3];
  //   Overflow = out_6; Zero = out_5

  // Notes on the sheet:
  //   Inputs
  //   ADD/SUB_Signal
  //   ArthOpSignal
  //   Operations
  //   data out
  //   zero_Detection
  //   outputs
endmodule

module LogicalUnit (
  input  [3:0] OperationControl,
  input  [31:0] RS1_RD,
  input  [31:0] RS2_imm32,
  output [31:0] out_4
);

  wire [31:0] AND, NOR, OR, XOR;

  assign AND = RS1_RD & RS2_imm32;  // AND_Gate and_1, 32 bits wide
  assign OR = RS1_RD | RS2_imm32;  // OR_Gate or_1, 32 bits wide
  assign XOR = RS1_RD ^ RS2_imm32;  // XOR_Gate xor_1, 32 bits wide
  assign NOR = ~OR;  // NOT_Gate not_1, 32 bits wide
  Multiplexer #(.select(2), .width(32), .enable("false")) multiplexer_1 (
    .in0(AND), .in1(OR), .in2(NOR), .in3(XOR), .out(out_4), .sel(OperationControl[1:0]));

  // Other names for the same wires on the sheet: A[31:0] = RS1_RD; B[31:0] = RS2_imm32;
  //   Result_Selection[1:0] = OperationControl[1:0]; ArthOp = OperationControl[2]; AluOp_1_bit = OperationControl[3]

  // Notes on the sheet:
  //   Inputs
  //   ADD/SUB_Signal
  //   ArthOpSignal
  //   Operations
  //   Output
endmodule

module extender (
  input  [15:0] in_1,
  input  in_2,
  output [31:0] out_3
);

  wire [31:0] bit_extender_1_out, bit_extender_2_out;

  assign bit_extender_1_out = {{16{1'b0}}, in_1};  // Bit_Extender bit_extender_1
  assign bit_extender_2_out = {{16{in_1[15]}}, in_1};  // Bit_Extender bit_extender_2
  Multiplexer #(.width(32)) multiplexer_1 (
    .in0(bit_extender_1_out), .in1(bit_extender_2_out), .out(out_3), .sel(in_2));  // open: en
endmodule

module MainControlUnit (
  input  [5:0] in_1,
  output jump,
  output branch,
  output [1:0] B_TYPE,
  output SignSlc,
  output SourceSlc,
  output RegWr,
  output B_Alu_slc,
  output [1:0] WB_SLC,
  output WrMemory,
  output ReadMemory
);

  wire and_2_out, and_3_out, and_4_out, and_5_out, and_6_out, and_7_out, and_8_out, and_11_out, and_12_out,
       and_13_out, not_1_out, not_2_out, not_3_out, not_4_out, not_5_out, not_6_out, not_7_out, not_8_out,
       not_9_out, not_10_out, not_11_out, not_12_out, not_13_out, not_14_out, not_15_out, not_16_out,
       not_17_out, not_18_out, not_19_out, not_20_out, not_21_out;

  and and_1 (jump, in_1[3], in_1[2], in_1[1], in_1[0]);
  and and_2 (and_2_out, in_1[4], in_1[1]);
  and and_3 (and_3_out, in_1[4], in_1[2]);
  not not_1 (not_1_out, in_1[3]);
  and and_4 (and_4_out, not_1_out, not_2_out);
  not not_2 (not_2_out, in_1[0]);
  not not_3 (not_3_out, in_1[2]);
  and and_5 (and_5_out, not_3_out, not_4_out, not_5_out);
  not not_4 (not_4_out, in_1[1]);
  not not_5 (not_5_out, in_1[0]);
  and and_6 (and_6_out, in_1[2], not_6_out, in_1[0]);
  not not_6 (not_6_out, in_1[1]);
  and and_7 (and_7_out, in_1[3], in_1[2], in_1[1]);
  not not_7 (not_7_out, in_1[0]);
  not not_8 (not_8_out, in_1[4]);
  not not_9 (not_9_out, in_1[2]);
  and and_8 (and_8_out, not_9_out, not_10_out, not_11_out);
  not not_10 (not_10_out, in_1[1]);
  not not_11 (not_11_out, in_1[0]);
  not not_12 (not_12_out, in_1[4]);
  not not_13 (not_13_out, in_1[3]);
  not not_14 (not_14_out, in_1[2]);
  not not_15 (not_15_out, in_1[1]);
  not not_16 (not_16_out, in_1[0]);
  and and_9 (WB_SLC[1], in_1[3], in_1[2], in_1[1], in_1[0]);
  not not_17 (not_17_out, in_1[2]);
  not not_18 (not_18_out, in_1[1]);
  not not_19 (not_19_out, in_1[2]);
  not not_20 (not_20_out, in_1[1]);
  not not_21 (not_21_out, in_1[0]);
  or or_1 (branch, and_2_out, and_3_out);
  or or_2 (SignSlc, and_4_out, and_5_out, and_6_out, and_7_out);
  and and_10 (SourceSlc, in_1[3], in_1[2], in_1[1], not_7_out);
  or or_3 (RegWr, not_8_out, and_8_out);
  and and_11 (and_11_out, not_12_out, not_13_out, not_14_out, not_15_out, not_16_out);
  and and_12 (and_12_out, in_1[4], in_1[1]);
  or or_4 (B_Alu_slc, and_11_out, and_12_out, and_13_out);
  and and_13 (and_13_out, in_1[4], in_1[2]);
  and and_14 (WrMemory, in_1[4], not_17_out, not_18_out, in_1[0]);
  and and_15 (ReadMemory, in_1[4], not_19_out, not_20_out, not_21_out);

  assign B_TYPE = {in_1[2], in_1[0]};
  assign WB_SLC[0] = in_1[4];

  // Notes on the sheet:
  //   op5
  //   op4
  //   op3
  //   op2
  //   op1
  //   op0
endmodule

module ALUOperation (
  input  [5:0] in_1,
  input  [10:0] in_2,
  output [5:0] out_3
);

  wire and_1_out, and_2_out, and_3_out, and_4_out, and_5_out, and_6_out, and_7_out, and_8_out, and_9_out,
       and_10_out, and_11_out, and_12_out, and_13_out, and_14_out, and_15_out, and_16_out, and_17_out,
       and_18_out, and_20_out, and_21_out, and_22_out, and_23_out, and_24_out, and_25_out, and_26_out,
       and_27_out, and_28_out, and_29_out, and_30_out, and_31_out, and_32_out, and_33_out, and_34_out,
       and_35_out, not_1_out, not_2_out, not_3_out, not_4_out, not_5_out, not_6_out, not_7_out, not_8_out,
       not_9_out, not_10_out, not_11_out, not_12_out, not_13_out, not_14_out, not_15_out, not_16_out,
       not_17_out, not_18_out, not_19_out, not_20_out, not_21_out, not_22_out, not_23_out, not_24_out,
       not_25_out, not_26_out, not_27_out, not_28_out, not_29_out, not_30_out, not_31_out, not_32_out,
       not_33_out, not_34_out, not_35_out, not_36_out, not_37_out, not_38_out, not_39_out, not_40_out,
       not_41_out, not_42_out, not_43_out, not_44_out, not_45_out, not_46_out, not_47_out, not_48_out,
       not_49_out, not_50_out, not_51_out, not_52_out, not_53_out, not_54_out, not_55_out, not_56_out,
       not_57_out, not_58_out, not_59_out, not_60_out, not_61_out, not_62_out, not_63_out, not_64_out,
       not_65_out, not_66_out, not_67_out, not_68_out, not_69_out, not_70_out, not_71_out, not_72_out,
       not_73_out, not_74_out, not_75_out, not_76_out, not_77_out, not_78_out, not_79_out, not_80_out,
       not_81_out, not_82_out, not_83_out, not_84_out, not_85_out, not_86_out, not_87_out, not_88_out,
       not_89_out, not_90_out, not_91_out, not_92_out, not_93_out, not_94_out, not_95_out, not_96_out,
       not_97_out, not_98_out, not_99_out;

  not not_1 (not_1_out, in_1[4]);
  not not_2 (not_2_out, in_1[3]);
  not not_3 (not_3_out, in_1[2]);
  not not_4 (not_4_out, in_1[1]);
  not not_5 (not_5_out, in_1[0]);
  not not_6 (not_6_out, in_2[2]);
  not not_7 (not_7_out, in_1[4]);
  not not_8 (not_8_out, in_1[3]);
  not not_9 (not_9_out, in_1[2]);
  not not_10 (not_10_out, in_1[1]);
  not not_11 (not_11_out, in_1[0]);
  not not_12 (not_12_out, in_1[4]);
  not not_13 (not_13_out, in_1[3]);
  not not_14 (not_14_out, in_1[2]);
  not not_15 (not_15_out, in_1[1]);
  not not_16 (not_16_out, in_1[0]);
  not not_17 (not_17_out, in_2[0]);
  not not_18 (not_18_out, in_1[2]);
  not not_19 (not_19_out, in_1[0]);
  not not_20 (not_20_out, in_1[1]);
  not not_21 (not_21_out, in_1[2]);
  not not_22 (not_22_out, in_1[1]);
  not not_23 (not_23_out, in_1[0]);
  not not_24 (not_24_out, in_2[3]);
  not not_25 (not_25_out, in_1[2]);
  not not_26 (not_26_out, in_1[1]);
  not not_27 (not_27_out, in_1[0]);
  not not_28 (not_28_out, in_1[2]);
  not not_29 (not_29_out, in_1[1]);
  not not_30 (not_30_out, in_1[0]);
  not not_31 (not_31_out, in_2[2]);
  not not_32 (not_32_out, in_2[1]);
  not not_33 (not_33_out, in_2[0]);
  not not_34 (not_34_out, in_1[2]);
  not not_35 (not_35_out, in_1[1]);
  not not_36 (not_36_out, in_1[0]);
  not not_37 (not_37_out, in_1[4]);
  not not_38 (not_38_out, in_1[0]);
  not not_39 (not_39_out, in_2[2]);
  not not_40 (not_40_out, in_1[4]);
  not not_41 (not_41_out, in_1[0]);
  not not_42 (not_42_out, in_1[4]);
  not not_43 (not_43_out, in_1[0]);
  not not_44 (not_44_out, in_1[3]);
  not not_45 (not_45_out, in_1[1]);
  not not_46 (not_46_out, in_1[4]);
  not not_47 (not_47_out, in_1[2]);
  not not_48 (not_48_out, in_1[4]);
  not not_49 (not_49_out, in_1[1]);
  not not_50 (not_50_out, in_1[0]);
  not not_51 (not_51_out, in_2[3]);
  not not_52 (not_52_out, in_2[2]);
  not not_53 (not_53_out, in_1[4]);
  not not_54 (not_54_out, in_1[1]);
  not not_55 (not_55_out, in_1[0]);
  not not_56 (not_56_out, in_2[3]);
  not not_57 (not_57_out, in_1[4]);
  not not_58 (not_58_out, in_1[1]);
  not not_59 (not_59_out, in_1[0]);
  not not_60 (not_60_out, in_2[2]);
  not not_61 (not_61_out, in_2[1]);
  not not_62 (not_62_out, in_1[4]);
  not not_63 (not_63_out, in_1[1]);
  not not_64 (not_64_out, in_1[0]);
  not not_65 (not_65_out, in_2[1]);
  not not_66 (not_66_out, in_2[0]);
  not not_67 (not_67_out, in_1[4]);
  not not_68 (not_68_out, in_1[3]);
  not not_69 (not_69_out, in_1[4]);
  not not_70 (not_70_out, in_1[1]);
  not not_71 (not_71_out, in_1[0]);
  not not_72 (not_72_out, in_1[1]);
  not not_73 (not_73_out, in_1[4]);
  not not_74 (not_74_out, in_1[3]);
  not not_75 (not_75_out, in_1[0]);
  not not_76 (not_76_out, in_2[3]);
  not not_77 (not_77_out, in_2[2]);
  not not_78 (not_78_out, in_1[4]);
  not not_79 (not_79_out, in_1[3]);
  not not_80 (not_80_out, in_1[0]);
  not not_81 (not_81_out, in_2[0]);
  not not_82 (not_82_out, in_1[4]);
  not not_83 (not_83_out, in_1[3]);
  not not_84 (not_84_out, in_1[0]);
  not not_85 (not_85_out, in_2[2]);
  not not_86 (not_86_out, in_2[1]);
  not not_87 (not_87_out, in_1[4]);
  not not_88 (not_88_out, in_1[3]);
  not not_89 (not_89_out, in_1[0]);
  not not_90 (not_90_out, in_2[2]);
  not not_91 (not_91_out, in_2[0]);
  not not_92 (not_92_out, in_1[4]);
  not not_93 (not_93_out, in_1[0]);
  not not_94 (not_94_out, in_1[3]);
  not not_95 (not_95_out, in_1[1]);
  not not_96 (not_96_out, in_1[0]);
  not not_97 (not_97_out, in_1[2]);
  not not_98 (not_98_out, in_1[1]);
  not not_99 (not_99_out, in_1[1]);
  and and_1 (and_1_out, not_1_out, not_2_out, not_3_out, not_4_out, not_5_out, in_2[3], not_6_out, in_2[0]);
  and and_2 (and_2_out, not_7_out, not_8_out, not_9_out, not_10_out, not_11_out, in_2[3], in_2[1]);
  and and_3 (and_3_out, not_12_out, not_13_out, not_14_out, not_15_out, not_16_out, in_2[3], in_2[2], not_17_out);
  and and_4 (and_4_out, in_1[3], not_18_out, in_1[0]);
  and and_5 (and_5_out, in_1[3], in_1[1], not_19_out);
  and and_6 (and_6_out, in_1[3], in_1[2], not_20_out);
  and and_7 (and_7_out, not_21_out, not_22_out, not_23_out, not_24_out, in_2[2]);
  and and_8 (and_8_out, not_25_out, not_26_out, not_27_out, in_2[2], in_2[0]);
  and and_9 (and_9_out, not_28_out, not_29_out, not_30_out, in_2[3], not_31_out, not_32_out, not_33_out);
  and and_10 (and_10_out, in_1[2], in_1[0]);
  and and_11 (and_11_out, in_1[2], in_1[1]);
  and and_12 (and_12_out, in_1[3], not_34_out, not_35_out, not_36_out);
  and and_13 (and_13_out, not_37_out, not_38_out, not_39_out);
  and and_14 (and_14_out, not_40_out, not_41_out, in_2[0]);
  and and_15 (and_15_out, not_42_out, not_43_out, in_2[1]);
  and and_16 (and_16_out, not_44_out, in_1[1]);
  and and_17 (and_17_out, in_1[3], not_45_out);
  and and_18 (and_18_out, in_1[4], in_1[2]);
  and and_19 (out_3[2], not_46_out, not_47_out, in_2[3]);
  and and_20 (and_20_out, not_48_out, not_49_out, not_50_out, not_51_out, not_52_out, in_2[1]);
  and and_21 (and_21_out, not_53_out, not_54_out, not_55_out, not_56_out, in_2[1], in_2[0]);
  and and_22 (and_22_out, not_57_out, not_58_out, not_59_out, in_2[3], not_60_out, not_61_out);
  and and_23 (and_23_out, not_62_out, not_63_out, not_64_out, in_2[3], not_65_out, not_66_out);
  and and_24 (and_24_out, not_67_out, not_68_out, in_1[1], in_1[0]);
  and and_25 (and_25_out, not_69_out, in_1[2], not_70_out, not_71_out);
  and and_26 (and_26_out, in_1[3], not_72_out);
  and and_27 (and_27_out, in_1[4], in_1[2], in_1[1]);
  and and_28 (and_28_out, not_73_out, not_74_out, not_75_out, not_76_out, not_77_out, in_2[0]);
  and and_29 (and_29_out, not_78_out, not_79_out, not_80_out, in_2[2], in_2[1], not_81_out);
  and and_30 (and_30_out, not_82_out, not_83_out, not_84_out, in_2[3], not_85_out, not_86_out);
  and and_31 (and_31_out, not_87_out, not_88_out, not_89_out, in_2[3], not_90_out, not_91_out);
  and and_32 (and_32_out, not_92_out, in_1[1], not_93_out);
  and and_33 (and_33_out, not_94_out, in_1[2], not_95_out, not_96_out);
  and and_34 (and_34_out, in_1[3], not_97_out, not_98_out);
  and and_35 (and_35_out, in_1[4], in_1[2], not_99_out);
  or or_1 (out_3[5], and_1_out, and_2_out, and_3_out, and_4_out, and_5_out, and_6_out);
  or or_2 (out_3[4], and_7_out, and_8_out, and_9_out, and_10_out, and_11_out, and_12_out, in_1[4]);
  or or_3 (out_3[3], and_13_out, and_14_out, and_15_out, and_16_out, and_17_out, and_18_out);
  or or_4 (out_3[1], and_20_out, and_21_out, and_22_out, and_23_out, and_24_out, and_25_out, and_26_out, and_27_out);
  or or_5 (out_3[0], and_28_out, and_29_out, and_30_out, and_31_out, and_32_out, and_33_out, and_34_out, and_35_out);
endmodule

module Imm_select (
  input  [5:0] in_1,
  output imm_slc
);

  wire and_1_out, not_1_out, not_2_out, not_3_out, not_4_out, not_5_out;

  not not_1 (not_1_out, in_1[3]);
  not not_2 (not_2_out, in_1[2]);
  not not_3 (not_3_out, in_1[1]);
  not not_4 (not_4_out, in_1[0]);
  not not_5 (not_5_out, in_1[4]);
  and and_1 (and_1_out, not_1_out, not_2_out, not_3_out, not_4_out);
  or or_1 (imm_slc, not_5_out, and_1_out);
endmodule

module Reg_File_Test (
  input  [4:0] RA,
  input  [4:0] RW,
  input  [31:0] BusW,
  input  RegWrite,
  input  [4:0] RB,
  input  in_6,
  output [31:0] out_7,
  output [31:0] out_8,
  output [31:0] out_9,
  output [31:0] out_10,
  output [31:0] out_11,
  output [31:0] out_12,
  output [31:0] out_13,
  output [31:0] out_14,
  output [31:0] out_15,
  output [31:0] out_16,
  output [31:0] out_17,
  output [31:0] out_18,
  output [31:0] out_19,
  output [31:0] out_20,
  output [31:0] out_21,
  output [31:0] out_22,
  output [31:0] out_23,
  output [31:0] BusA,
  output [31:0] BusB,
  output [31:0] out_26,
  output [31:0] out_27,
  output [31:0] out_28,
  output [31:0] out_29,
  output [31:0] out_30,
  output [31:0] out_31,
  output [31:0] out_32,
  output [31:0] out_33,
  output [31:0] out_34,
  output [31:0] out_35,
  output [31:0] out_36,
  output [31:0] out_37,
  output [31:0] out_38,
  output [31:0] out_39,
  output [31:0] out_40
);

  wire IEn0, IEn1, IEn2, IEn3, IEn4, IEn5, IEn6, IEn7, IEn8, IEn9, IEn10, IEn11, IEn12, IEn13, IEn14, IEn15,
       IEn16, IEn17, IEn18, IEn19, IEn20, IEn21, IEn22, IEn23, IEn24, IEn25, IEn26, IEn27, IEn28, IEn29,
       IEn30, IEn31, InputR0, InputR1, InputR2, InputR3, InputR4, InputR5, InputR6, InputR7, InputR8,
       InputR9, InputR10, InputR11, InputR12, InputR13, InputR14, InputR15, InputR16, InputR17, InputR18,
       InputR19, InputR20, InputR21, InputR22, InputR23, InputR24, InputR25, InputR26, InputR27, InputR28,
       InputR29, InputR30, InputR31;

  Decoder #(.select(5), .enable("false")) decoder_1 (
    .out0(InputR0), .out1(InputR1), .out2(InputR2), .out3(InputR3), .out4(InputR4), .out5(InputR5),
    .out6(InputR6), .out7(InputR7), .out8(InputR8), .out9(InputR9), .out10(InputR10), .out11(InputR11),
    .out12(InputR12), .out13(InputR13), .out14(InputR14), .out15(InputR15), .out16(InputR16),
    .out17(InputR17), .out18(InputR18), .out19(InputR19), .out20(InputR20), .out21(InputR21),
    .out22(InputR22), .out23(InputR23), .out24(InputR24), .out25(InputR25), .out26(InputR26),
    .out27(InputR27), .out28(InputR28), .out29(InputR29), .out30(InputR30), .out31(InputR31), .sel(RW));
  and and_1 (IEn0, RegWrite, RegWrite, InputR0, InputR0);
  and and_2 (IEn4, RegWrite, RegWrite, InputR4, InputR4);
  and and_3 (IEn8, RegWrite, RegWrite, InputR8, InputR8);
  and and_4 (IEn12, RegWrite, RegWrite, InputR12, InputR12);
  and and_5 (IEn16, RegWrite, RegWrite, InputR16, InputR16);
  and and_6 (IEn20, RegWrite, RegWrite, InputR20, InputR20);
  and and_7 (IEn24, RegWrite, RegWrite, InputR24, InputR24);
  and and_8 (IEn28, RegWrite, RegWrite, InputR28, InputR28);
  Register #(.width(32)) R0 (.D({32{1'b0}}), .en(IEn0), .Q(out_7), .clk(in_6));  // open: clr
  Register #(.width(32)) R4 (.D(BusW), .en(IEn4), .Q(out_20), .clk(in_6));  // open: clr
  Register #(.width(32)) R8 (.D(BusW), .en(IEn8), .Q(out_16), .clk(in_6));  // open: clr
  Register #(.width(32)) R12 (.D(BusW), .en(IEn12), .Q(out_12), .clk(in_6));  // open: clr
  Register #(.width(32)) R16 (.D(BusW), .en(IEn16), .Q(out_8), .clk(in_6));  // open: clr
  Register #(.width(32)) R20 (.D(BusW), .en(IEn20), .Q(out_37), .clk(in_6));  // open: clr
  Register #(.width(32)) R24 (.D(BusW), .en(IEn24), .Q(out_33), .clk(in_6));  // open: clr
  Register #(.width(32)) R28 (.D(BusW), .en(IEn28), .Q(out_29), .clk(in_6));  // open: clr
  and and_9 (IEn1, RegWrite, RegWrite, InputR1, InputR1);
  and and_10 (IEn5, RegWrite, RegWrite, InputR5, InputR5);
  and and_11 (IEn9, RegWrite, RegWrite, InputR9, InputR9);
  and and_12 (IEn13, RegWrite, RegWrite, InputR13, InputR13);
  and and_13 (IEn17, RegWrite, RegWrite, InputR17, InputR17);
  and and_14 (IEn21, RegWrite, RegWrite, InputR21, InputR21);
  and and_15 (IEn25, RegWrite, RegWrite, InputR25, InputR25);
  and and_16 (IEn29, RegWrite, RegWrite, InputR29, InputR29);
  Register #(.width(32)) R1 (.D(BusW), .en(IEn1), .Q(out_23), .clk(in_6));  // open: clr
  Register #(.width(32)) R5 (.D(BusW), .en(IEn5), .Q(out_19), .clk(in_6));  // open: clr
  Register #(.width(32)) R9 (.D(BusW), .en(IEn9), .Q(out_15), .clk(in_6));  // open: clr
  Register #(.width(32)) R13 (.D(BusW), .en(IEn13), .Q(out_11), .clk(in_6));  // open: clr
  Register #(.width(32)) R17 (.D(BusW), .en(IEn17), .Q(out_40), .clk(in_6));  // open: clr
  Register #(.width(32)) R21 (.D(BusW), .en(IEn21), .Q(out_36), .clk(in_6));  // open: clr
  Register #(.width(32)) R25 (.D(BusW), .en(IEn25), .Q(out_32), .clk(in_6));  // open: clr
  Register #(.width(32)) R29 (.D(BusW), .en(IEn29), .Q(out_28), .clk(in_6));  // open: clr
  and and_17 (IEn2, RegWrite, RegWrite, InputR2, InputR2);
  and and_18 (IEn6, RegWrite, RegWrite, InputR6, InputR6);
  and and_19 (IEn10, RegWrite, RegWrite, InputR10, InputR10);
  and and_20 (IEn14, RegWrite, RegWrite, InputR14, InputR14);
  and and_21 (IEn18, RegWrite, RegWrite, InputR18, InputR18);
  and and_22 (IEn22, RegWrite, RegWrite, InputR22, InputR22);
  and and_23 (IEn26, RegWrite, RegWrite, InputR26, InputR26);
  and and_24 (IEn30, RegWrite, RegWrite, InputR30, InputR30);
  Register #(.width(32)) R2 (.D(BusW), .en(IEn2), .Q(out_22), .clk(in_6));  // open: clr
  Register #(.width(32)) R6 (.D(BusW), .en(IEn6), .Q(out_18), .clk(in_6));  // open: clr
  Register #(.width(32)) R10 (.D(BusW), .en(IEn10), .Q(out_14), .clk(in_6));  // open: clr
  Register #(.width(32)) R14 (.D(BusW), .en(IEn14), .Q(out_10), .clk(in_6));  // open: clr
  Register #(.width(32)) R18 (.D(BusW), .en(IEn18), .Q(out_39), .clk(in_6));  // open: clr
  Register #(.width(32)) R22 (.D(BusW), .en(IEn22), .Q(out_35), .clk(in_6));  // open: clr
  Register #(.width(32)) R26 (.D(BusW), .en(IEn26), .Q(out_31), .clk(in_6));  // open: clr
  Register #(.width(32)) R30 (.D(BusW), .en(IEn30), .Q(out_27), .clk(in_6));  // open: clr
  and and_25 (IEn3, RegWrite, RegWrite, InputR3, InputR3);
  and and_26 (IEn7, RegWrite, RegWrite, InputR7, InputR7);
  and and_27 (IEn11, RegWrite, RegWrite, InputR11, InputR11);
  and and_28 (IEn15, RegWrite, RegWrite, InputR15, InputR15);
  and and_29 (IEn19, RegWrite, RegWrite, InputR19, InputR19);
  and and_30 (IEn23, RegWrite, RegWrite, InputR23, InputR23);
  and and_31 (IEn27, RegWrite, RegWrite, InputR27, InputR27);
  and and_32 (IEn31, RegWrite, RegWrite, InputR31, InputR31);
  Register #(.width(32)) R3 (.D(BusW), .en(IEn3), .Q(out_21), .clk(in_6));  // open: clr
  Register #(.width(32)) R7 (.D(BusW), .en(IEn7), .Q(out_17), .clk(in_6));  // open: clr
  Register #(.width(32)) R11 (.D(BusW), .en(IEn11), .Q(out_13), .clk(in_6));  // open: clr
  Register #(.width(32)) R15 (.D(BusW), .en(IEn15), .Q(out_9), .clk(in_6));  // open: clr
  Register #(.width(32)) R19 (.D(BusW), .en(IEn19), .Q(out_38), .clk(in_6));  // open: clr
  Register #(.width(32)) R23 (.D(BusW), .en(IEn23), .Q(out_34), .clk(in_6));  // open: clr
  Register #(.width(32)) R27 (.D(BusW), .en(IEn27), .Q(out_30), .clk(in_6));  // open: clr
  Register #(.width(32)) R31 (.D(BusW), .en(IEn31), .Q(out_26), .clk(in_6));  // open: clr
  Multiplexer #(.select(5), .width(32), .enable("false")) multiplexer_1 (
    .in0(out_7), .in1(out_23), .in2(out_22), .in3(out_21), .in4(out_20), .in5(out_19), .in6(out_18),
    .in7(out_17), .in8(out_16), .in9(out_15), .in10(out_14), .in11(out_13), .in12(out_12), .in13(out_11),
    .in14(out_10), .in15(out_9), .in16(out_8), .in17(out_40), .in18(out_39), .in19(out_38), .in20(out_37),
    .in21(out_36), .in22(out_35), .in23(out_34), .in24(out_33), .in25(out_32), .in26(out_31), .in27(out_30),
    .in28(out_29), .in29(out_28), .in30(out_27), .in31(out_26), .out(BusA), .sel(RA));
  Multiplexer #(.select(5), .width(32), .enable("false")) multiplexer_2 (
    .in0(out_7), .in1(out_23), .in2(out_22), .in3(out_21), .in4(out_20), .in5(out_19), .in6(out_18),
    .in7(out_17), .in8(out_16), .in9(out_15), .in10(out_14), .in11(out_13), .in12(out_12), .in13(out_11),
    .in14(out_10), .in15(out_9), .in16(out_8), .in17(out_40), .in18(out_39), .in19(out_38), .in20(out_37),
    .in21(out_36), .in22(out_35), .in23(out_34), .in24(out_33), .in25(out_32), .in26(out_31), .in27(out_30),
    .in28(out_29), .in29(out_28), .in30(out_27), .in31(out_26), .out(BusB), .sel(RB));

  // Other names for the same wires on the sheet: clck = in_6; DataIn[31:0] = BusW; DataOut0[31:0] = out_7;
  //   DataOut1[31:0] = out_23; DataOut2[31:0] = out_22; DataOut3[31:0] = out_21; DataOut4[31:0] = out_20;
  //   DataOut5[31:0] = out_19; DataOut6[31:0] = out_18; DataOut7[31:0] = out_17; DataOut8[31:0] = out_16;
  //   DataOut9[31:0] = out_15; DataOut10[31:0] = out_14; DataOut11[31:0] = out_13; DataOut12[31:0] = out_12;
  //   DataOut13[31:0] = out_11; DataOut14[31:0] = out_10; DataOut15[31:0] = out_9; DataOut16[31:0] = out_8;
  //   DataOut17[31:0] = out_40; DataOut18[31:0] = out_39; DataOut19[31:0] = out_38; DataOut20[31:0] = out_37;
  //   DataOut21[31:0] = out_36; DataOut22[31:0] = out_35; DataOut23[31:0] = out_34; DataOut24[31:0] = out_33;
  //   DataOut25[31:0] = out_32; DataOut26[31:0] = out_31; DataOut27[31:0] = out_30; DataOut28[31:0] = out_29;
  //   DataOut29[31:0] = out_28; DataOut30[31:0] = out_27; DataOut31[31:0] = out_26; Write = RegWrite
endmodule
