// Logisim project Registers.circ as structural Verilog: 2 circuits, main circuit main
module main (
  input  [4:0] in_1,
  input  [4:0] in_2,
  input  [4:0] in_3,
  input  in_4,
  input  [31:0] in_5,
  output [31:0] out_6,
  output [31:0] out_7
);

  wire clock_1_out;

  Clock clock_1 (.out(clock_1_out));
  Registers registers_1 (
    .RA(in_1), .RB(in_2), .BusA(out_6), .BusB(out_7), .RW(in_3), .RegWrite(in_4), .BusW(in_5),
    .in_6(clock_1_out));
endmodule

module Registers (
  input  [4:0] RA,
  input  [4:0] RW,
  input  [31:0] BusW,
  input  RegWrite,
  input  [4:0] RB,
  input  in_6,
  output [31:0] BusA,
  output [31:0] BusB
);

  wire IEn0, IEn1, IEn2, IEn3, IEn4, IEn5, IEn6, IEn7, IEn8, IEn9, IEn10, IEn11, IEn12, IEn13, IEn14, IEn15,
       IEn16, IEn17, IEn18, IEn19, IEn20, IEn21, IEn22, IEn23, IEn24, IEn25, IEn26, IEn27, IEn28, IEn29,
       IEn30, IEn31, InputR0, InputR1, InputR2, InputR3, InputR4, InputR5, InputR6, InputR7, InputR8,
       InputR9, InputR10, InputR11, InputR12, InputR13, InputR14, InputR15, InputR16, InputR17, InputR18,
       InputR19, InputR20, InputR21, InputR22, InputR23, InputR24, InputR25, InputR26, InputR27, InputR28,
       InputR29, InputR30, InputR31;
  wire [31:0] DataOut0, DataOut1, DataOut2, DataOut3, DataOut4, DataOut5, DataOut6, DataOut7, DataOut8,
       DataOut9, DataOut10, DataOut11, DataOut12, DataOut13, DataOut14, DataOut15, DataOut16, DataOut17,
       DataOut18, DataOut19, DataOut20, DataOut21, DataOut22, DataOut23, DataOut24, DataOut25, DataOut26,
       DataOut27, DataOut28, DataOut29, DataOut30, DataOut31;

  Decoder #(.select(5), .enable("false")) decoder_1 (
    .out0(InputR0), .out1(InputR1), .out2(InputR2), .out3(InputR3), .out4(InputR4), .out5(InputR5),
    .out6(InputR6), .out7(InputR7), .out8(InputR8), .out9(InputR9), .out10(InputR10), .out11(InputR11),
    .out12(InputR12), .out13(InputR13), .out14(InputR14), .out15(InputR15), .out16(InputR16),
    .out17(InputR17), .out18(InputR18), .out19(InputR19), .out20(InputR20), .out21(InputR21),
    .out22(InputR22), .out23(InputR23), .out24(InputR24), .out25(InputR25), .out26(InputR26),
    .out27(InputR27), .out28(InputR28), .out29(InputR29), .out30(InputR30), .out31(InputR31), .sel(RW));
  and and_1 (IEn0, RegWrite, RegWrite, InputR0, InputR0);
  and and_2 (IEn4, RegWrite, RegWrite, InputR4, InputR4);
  and and_3 (IEn8, RegWrite, RegWrite, InputR8, InputR8);
  and and_4 (IEn12, RegWrite, RegWrite, InputR12, InputR12);
  and and_5 (IEn16, RegWrite, RegWrite, InputR16, InputR16);
  and and_6 (IEn20, RegWrite, RegWrite, InputR20, InputR20);
  and and_7 (IEn24, RegWrite, RegWrite, InputR24, InputR24);
  and and_8 (IEn28, RegWrite, RegWrite, InputR28, InputR28);
  Register #(.width(32)) R0 (.D({32{1'b0}}), .en(IEn0), .Q(DataOut0), .clk(in_6));  // open: clr
  Register #(.width(32)) R4 (.D(BusW), .en(IEn4), .Q(DataOut4), .clk(in_6));  // open: clr
  Register #(.width(32)) R8 (.D(BusW), .en(IEn8), .Q(DataOut8), .clk(in_6));  // open: clr
  Register #(.width(32)) R12 (.D(BusW), .en(IEn12), .Q(DataOut12), .clk(in_6));  // open: clr
  Register #(.width(32)) R16 (.D(BusW), .en(IEn16), .Q(DataOut16), .clk(in_6));  // open: clr
  Register #(.width(32)) R20 (.D(BusW), .en(IEn20), .Q(DataOut20), .clk(in_6));  // open: clr
  Register #(.width(32)) R24 (.D(BusW), .en(IEn24), .Q(DataOut24), .clk(in_6));  // open: clr
  Register #(.width(32)) R28 (.D(BusW), .en(IEn28), .Q(DataOut28), .clk(in_6));  // open: clr
  and and_9 (IEn1, RegWrite, RegWrite, InputR1, InputR1);
  and and_10 (IEn5, RegWrite, RegWrite, InputR5, InputR5);
  and and_11 (IEn9, RegWrite, RegWrite, InputR9, InputR9);
  and and_12 (IEn13, RegWrite, RegWrite, InputR13, InputR13);
  and and_13 (IEn17, RegWrite, RegWrite, InputR17, InputR17);
  and and_14 (IEn21, RegWrite, RegWrite, InputR21, InputR21);
  and and_15 (IEn25, RegWrite, RegWrite, InputR25, InputR25);
  and and_16 (IEn29, RegWrite, RegWrite, InputR29, InputR29);
  Register #(.width(32)) R1 (.D(BusW), .en(IEn1), .Q(DataOut1), .clk(in_6));  // open: clr
  Register #(.width(32)) R5 (.D(BusW), .en(IEn5), .Q(DataOut5), .clk(in_6));  // open: clr
  Register #(.width(32)) R9 (.D(BusW), .en(IEn9), .Q(DataOut9), .clk(in_6));  // open: clr
  Register #(.width(32)) R13 (.D(BusW), .en(IEn13), .Q(DataOut13), .clk(in_6));  // open: clr
  Register #(.width(32)) R17 (.D(BusW), .en(IEn17), .Q(DataOut17), .clk(in_6));  // open: clr
  Register #(.width(32)) R21 (.D(BusW), .en(IEn21), .Q(DataOut21), .clk(in_6));  // open: clr
  Register #(.width(32)) R25 (.D(BusW), .en(IEn25), .Q(DataOut25), .clk(in_6));  // open: clr
  Register #(.width(32)) R29 (.D(BusW), .en(IEn29), .Q(DataOut29), .clk(in_6));  // open: clr
  and and_17 (IEn2, RegWrite, RegWrite, InputR2, InputR2);
  and and_18 (IEn6, RegWrite, RegWrite, InputR6, InputR6);
  and and_19 (IEn10, RegWrite, RegWrite, InputR10, InputR10);
  and and_20 (IEn14, RegWrite, RegWrite, InputR14, InputR14);
  and and_21 (IEn18, RegWrite, RegWrite, InputR18, InputR18);
  and and_22 (IEn22, RegWrite, RegWrite, InputR22, InputR22);
  and and_23 (IEn26, RegWrite, RegWrite, InputR26, InputR26);
  and and_24 (IEn30, RegWrite, RegWrite, InputR30, InputR30);
  Register #(.width(32)) R2 (.D(BusW), .en(IEn2), .Q(DataOut2), .clk(in_6));  // open: clr
  Register #(.width(32)) R6 (.D(BusW), .en(IEn6), .Q(DataOut6), .clk(in_6));  // open: clr
  Register #(.width(32)) R10 (.D(BusW), .en(IEn10), .Q(DataOut10), .clk(in_6));  // open: clr
  Register #(.width(32)) R14 (.D(BusW), .en(IEn14), .Q(DataOut14), .clk(in_6));  // open: clr
  Register #(.width(32)) R18 (.D(BusW), .en(IEn18), .Q(DataOut18), .clk(in_6));  // open: clr
  Register #(.width(32)) R22 (.D(BusW), .en(IEn22), .Q(DataOut22), .clk(in_6));  // open: clr
  Register #(.width(32)) R26 (.D(BusW), .en(IEn26), .Q(DataOut26), .clk(in_6));  // open: clr
  Register #(.width(32)) R30 (.D(BusW), .en(IEn30), .Q(DataOut30), .clk(in_6));  // open: clr
  and and_25 (IEn3, RegWrite, RegWrite, InputR3, InputR3);
  and and_26 (IEn7, RegWrite, RegWrite, InputR7, InputR7);
  and and_27 (IEn11, RegWrite, RegWrite, InputR11, InputR11);
  and and_28 (IEn15, RegWrite, RegWrite, InputR15, InputR15);
  and and_29 (IEn19, RegWrite, RegWrite, InputR19, InputR19);
  and and_30 (IEn23, RegWrite, RegWrite, InputR23, InputR23);
  and and_31 (IEn27, RegWrite, RegWrite, InputR27, InputR27);
  and and_32 (IEn31, RegWrite, RegWrite, InputR31, InputR31);
  Register #(.width(32)) R3 (.D(BusW), .en(IEn3), .Q(DataOut3), .clk(in_6));  // open: clr
  Register #(.width(32)) R7 (.D(BusW), .en(IEn7), .Q(DataOut7), .clk(in_6));  // open: clr
  Register #(.width(32)) R11 (.D(BusW), .en(IEn11), .Q(DataOut11), .clk(in_6));  // open: clr
  Register #(.width(32)) R15 (.D(BusW), .en(IEn15), .Q(DataOut15), .clk(in_6));  // open: clr
  Register #(.width(32)) R19 (.D(BusW), .en(IEn19), .Q(DataOut19), .clk(in_6));  // open: clr
  Register #(.width(32)) R23 (.D(BusW), .en(IEn23), .Q(DataOut23), .clk(in_6));  // open: clr
  Register #(.width(32)) R27 (.D(BusW), .en(IEn27), .Q(DataOut27), .clk(in_6));  // open: clr
  Register #(.width(32)) R31 (.D(BusW), .en(IEn31), .Q(DataOut31), .clk(in_6));  // open: clr
  Multiplexer #(.select(5), .width(32), .enable("false")) multiplexer_1 (
    .in0(DataOut0), .in1(DataOut1), .in2(DataOut2), .in3(DataOut3), .in4(DataOut4), .in5(DataOut5),
    .in6(DataOut6), .in7(DataOut7), .in8(DataOut8), .in9(DataOut9), .in10(DataOut10), .in11(DataOut11),
    .in12(DataOut12), .in13(DataOut13), .in14(DataOut14), .in15(DataOut15), .in16(DataOut16),
    .in17(DataOut17), .in18(DataOut18), .in19(DataOut19), .in20(DataOut20), .in21(DataOut21),
    .in22(DataOut22), .in23(DataOut23), .in24(DataOut24), .in25(DataOut25), .in26(DataOut26),
    .in27(DataOut27), .in28(DataOut28), .in29(DataOut29), .in30(DataOut30), .in31(DataOut31), .out(BusA),
    .sel(RA));
  Multiplexer #(.select(5), .width(32), .enable("false")) multiplexer_2 (
    .in0(DataOut0), .in1(DataOut1), .in2(DataOut2), .in3(DataOut3), .in4(DataOut4), .in5(DataOut5),
    .in6(DataOut6), .in7(DataOut7), .in8(DataOut8), .in9(DataOut9), .in10(DataOut10), .in11(DataOut11),
    .in12(DataOut12), .in13(DataOut13), .in14(DataOut14), .in15(DataOut15), .in16(DataOut16),
    .in17(DataOut17), .in18(DataOut18), .in19(DataOut19), .in20(DataOut20), .in21(DataOut21),
    .in22(DataOut22), .in23(DataOut23), .in24(DataOut24), .in25(DataOut25), .in26(DataOut26),
    .in27(DataOut27), .in28(DataOut28), .in29(DataOut29), .in30(DataOut30), .in31(DataOut31), .out(BusB),
    .sel(RB));

  // Other names for the same wires on the sheet: clck = in_6; DataIn[31:0] = BusW; Write = RegWrite
endmodule
