// Logisim project ShifterUnit.circ as structural Verilog: 2 circuits, main circuit main
module main (
);

  Shift shift_1 ();  // open: in_2, out_4, OperationControl, in_3
endmodule

module Shift (
  input  [3:0] OperationControl,
  input  [31:0] in_2,
  input  [31:0] in_3,
  output [31:0] out_4
);

  wire [31:0] Arhimetic_Right, Logical_Left, Logical_Right, Rotate_Right;

  Shifter #(.width(32)) shifter_1 (.in(in_2), .\dist (in_3[4:0]), .out(Logical_Left));
  Shifter #(.width(32), .shift("lr")) shifter_2 (.in(in_2), .\dist (in_3[4:0]), .out(Logical_Right));
  Shifter #(.width(32), .shift("ar")) shifter_3 (.in(in_2), .\dist (in_3[4:0]), .out(Arhimetic_Right));
  Shifter #(.width(32), .shift("rr")) shifter_4 (.in(in_2), .\dist (in_3[4:0]), .out(Rotate_Right));
  Multiplexer #(.select(2), .width(32), .enable("false")) multiplexer_1 (
    .in0(Logical_Left), .in1(Logical_Right), .in2(Arhimetic_Right), .in3(Rotate_Right), .out(out_4),
    .sel(OperationControl[1:0]));

  // Other names for the same wires on the sheet: A[31:0] = in_2; Shift_Amount[4:0] = in_3[4:0];
  //   Result_Selection[1:0] = OperationControl[1:0]; ArthOp = OperationControl[2]; AluOp_1_bit = OperationControl[3]

  // Notes on the sheet:
  //   Inputs
  //   ADD/SUB_Signal
  //   ArthOpSignal
  //   Operations
  //   Output
endmodule
